// Logisim project FISC_V (3) (2) (2) (9) (4).circ as structural Verilog
module ALU (
  input  [31:0] dataA,
  input  [31:0] dataB,
  input  [3:0] Selector,
  output [31:0] dataD,
  output zf
);

  wire comparator_1_lt, comparator_2_lt;
  wire [31:0] addOut, andOut, orOut, sllOut, sltOut, sltuOut, sraOut, srlOut, subOut, xorOut;

  Adder #(.width(32)) adder_1 (.a(dataA), .b(dataB), .out(addOut));  // open: cin, cout
  Subtractor #(.width(32)) subtractor_1 (.a(dataA), .b(dataB), .out(subOut));  // open: bin, bout
  Shifter #(.width(32)) shifter_1 (.in(dataA), .\dist (dataB[4:0]), .out(sllOut));
  Comparator #(.width(32)) comparator_1 (.a(dataA), .b(dataB), .lt(comparator_1_lt));  // open: gt, eq
  Comparator #(.mode("unsigned"), .width(32)) comparator_2 (
    .a(dataA), .b(dataB), .lt(comparator_2_lt));  // open: gt, eq
  assign xorOut = dataA ^ dataB;  // XOR_Gate xor_1, 32 bits wide
  Shifter #(.shift("lr"), .width(32)) shifter_2 (.in(dataA), .\dist (dataB[4:0]), .out(srlOut));
  Shifter #(.shift("ar"), .width(32)) shifter_3 (.in(dataA), .\dist (dataB[4:0]), .out(sraOut));
  assign orOut = dataA | dataB;  // OR_Gate or_1, 32 bits wide
  assign andOut = dataA & dataB;  // AND_Gate and_1, 32 bits wide
  assign sltOut = {{31{1'b0}}, comparator_1_lt};  // Bit_Extender bit_extender_1
  assign sltuOut = {{31{comparator_2_lt}}, comparator_2_lt};  // Bit_Extender bit_extender_2
  Multiplexer #(.select(4), .width(32)) multiplexer_1 (
    .in0(addOut), .in1(sllOut), .in2(sltOut), .in3(sltuOut), .in4(xorOut), .in5(srlOut), .in6(orOut),
    .in7(andOut), .in8(subOut), .in13(sraOut), .out(dataD), .sel(Selector));  // open: in9, in10, in11, in12, in14, in15
  nor nor_1 (zf, dataD[0], dataD[1], dataD[2], dataD[3], dataD[4], dataD[5], dataD[6], dataD[7], dataD[8], dataD[9], dataD[10], dataD[11], dataD[12], dataD[13], dataD[14], dataD[15], dataD[16], dataD[17], dataD[18], dataD[19], dataD[20], dataD[21], dataD[22], dataD[23], dataD[24], dataD[25], dataD[26], dataD[27], dataD[28], dataD[29], dataD[30], dataD[31]);

  // Other names for the same wires on the sheet: dataBL5[4:0] = dataB[4:0]; dataD_T[31:0] = dataD;
  //   Selector_T[3:0] = Selector

  // Notes on the sheet:
  //   0000 add
  //   1000 sub
  //   دستورات مربوط به ALU
  //   0001 sll - Shift Left Logical
  //   0010 slt - Set Less Than
  //   0011 sltu - Set Less Than Unsigned
  //   0100 xor - eXclusive OR
  //   0101 srl - Shift Right Logical
  //   1101 sra - Shift Right Arithmetic
  //   0110 or - Logical OR
  //   0111 and - Logical AND
endmodule

module RegisterFile (
  input  [4:0] rsi1,
  input  [4:0] rsi2,
  input  [4:0] rdi,
  input  wena,
  input  clk,
  input  [31:0] rd_Value,
  output [31:0] rs1,
  output [31:0] rs2
);

  wire x0we_t, x1we_t, x2we_t, x3we_t, x4we_t, x5we_t, x6we_t, x7we_t, x8we_t, x9we_t, x10we_t, x11we_t,
       x12we_t, x13we_t, x14we_t, x15we_t, x16we_t, x17we_t, x18we_t, x19we_t, x20we_t, x21we_t, x22we_t,
       x23we_t, x24we_t, x25we_t, x26we_t, x27we_t, x28we_t, x29we_t, x30we_t, x31we_t;
  wire [31:0] x0q, x1q, x2q, x3q, x4q, x5q, x6q, x7q, x8q, x9q, x10q, x11q, x12q, x13q, x14q, x15q, x16q,
       x17q, x18q, x19q, x20q, x21q, x22q, x23q, x24q, x25q, x26q, x27q, x28q, x29q, x30q, X31q, x31q_t;

  Demultiplexer #(.select(5)) demultiplexer_1 (
    .out0(x0we_t), .out1(x1we_t), .out2(x2we_t), .out3(x3we_t), .out4(x4we_t), .out5(x5we_t), .out6(x6we_t),
    .out7(x7we_t), .out8(x8we_t), .out9(x9we_t), .out10(x10we_t), .out11(x11we_t), .out12(x12we_t),
    .out13(x13we_t), .out14(x14we_t), .out15(x15we_t), .out16(x16we_t), .out17(x17we_t), .out18(x18we_t),
    .out19(x19we_t), .out20(x20we_t), .out21(x21we_t), .out22(x22we_t), .out23(x23we_t), .out24(x24we_t),
    .out25(x25we_t), .out26(x26we_t), .out27(x27we_t), .out28(x28we_t), .out29(x29we_t), .out30(x30we_t),
    .out31(x31we_t), .in(wena), .sel(rdi));
  Register #(.width(32)) x0 (.D({32{1'b0}}), .en(x0we_t), .clk(clk), .Q(x0q));  // open: clr
  Register #(.width(32)) x4 (.D(rd_Value), .en(x4we_t), .clk(clk), .Q(x4q));  // open: clr
  Register #(.width(32)) x8 (.D(rd_Value), .en(x8we_t), .clk(clk), .Q(x8q));  // open: clr
  Register #(.width(32)) x12 (.D(rd_Value), .en(x12we_t), .clk(clk), .Q(x12q));  // open: clr
  Register #(.width(32)) x16 (.D(rd_Value), .en(x16we_t), .clk(clk), .Q(x16q));  // open: clr
  Register #(.width(32)) x20 (.D(rd_Value), .en(x20we_t), .clk(clk), .Q(x20q));  // open: clr
  Register #(.width(32)) x24 (.D(rd_Value), .en(x24we_t), .clk(clk), .Q(x24q));  // open: clr
  Register #(.width(32)) x28 (.D(rd_Value), .en(x28we_t), .clk(clk), .Q(x28q));  // open: clr
  Register #(.width(32)) x1 (.D(rd_Value), .en(x1we_t), .clk(clk), .Q(x1q));  // open: clr
  Register #(.width(32)) x5 (.D(rd_Value), .en(x5we_t), .clk(clk), .Q(x5q));  // open: clr
  Register #(.width(32)) x9 (.D(rd_Value), .en(x9we_t), .clk(clk), .Q(x9q));  // open: clr
  Register #(.width(32)) x13 (.D(rd_Value), .en(x13we_t), .clk(clk), .Q(x13q));  // open: clr
  Register #(.width(32)) x17 (.D(rd_Value), .en(x17we_t), .clk(clk), .Q(x17q));  // open: clr
  Register #(.width(32)) x21 (.D(rd_Value), .en(x21we_t), .clk(clk), .Q(x21q));  // open: clr
  Register #(.width(32)) x25 (.D(rd_Value), .en(x25we_t), .clk(clk), .Q(x25q));  // open: clr
  Register #(.width(32)) x29 (.D(rd_Value), .en(x29we_t), .clk(clk), .Q(x29q));  // open: clr
  Register #(.width(32)) x2 (.D(rd_Value), .en(x2we_t), .clk(clk), .Q(x2q));  // open: clr
  Register #(.width(32)) x6 (.D(rd_Value), .en(x6we_t), .clk(clk), .Q(x6q));  // open: clr
  Register #(.width(32)) x10 (.D(rd_Value), .en(x10we_t), .clk(clk), .Q(x10q));  // open: clr
  Register #(.width(32)) x14 (.D(rd_Value), .en(x14we_t), .clk(clk), .Q(x14q));  // open: clr
  Register #(.width(32)) x18 (.D(rd_Value), .en(x18we_t), .clk(clk), .Q(x18q));  // open: clr
  Register #(.width(32)) x22 (.D(rd_Value), .en(x22we_t), .clk(clk), .Q(x22q));  // open: clr
  Register #(.width(32)) x26 (.D(rd_Value), .en(x26we_t), .clk(clk), .Q(x26q));  // open: clr
  Register #(.width(32)) x30 (.D(rd_Value), .en(x30we_t), .clk(clk), .Q(x30q));  // open: clr
  Register #(.width(32)) x3 (.D(rd_Value), .en(x3we_t), .clk(clk), .Q(x3q));  // open: clr
  Register #(.width(32)) x7 (.D(rd_Value), .en(x7we_t), .clk(clk), .Q(x7q));  // open: clr
  Register #(.width(32)) x11 (.D(rd_Value), .en(x11we_t), .clk(clk), .Q(x11q));  // open: clr
  Register #(.width(32)) x15 (.D(rd_Value), .en(x15we_t), .clk(clk), .Q(x15q));  // open: clr
  Register #(.width(32)) x19 (.D(rd_Value), .en(x19we_t), .clk(clk), .Q(x19q));  // open: clr
  Register #(.width(32)) x23 (.D(rd_Value), .en(x23we_t), .clk(clk), .Q(x23q));  // open: clr
  Register #(.width(32)) x27 (.D(rd_Value), .en(x27we_t), .clk(clk), .Q(x27q));  // open: clr
  Register #(.width(32)) X31 (.D(rd_Value), .en(x31we_t), .clk(clk), .Q(X31q));  // open: clr
  Multiplexer #(.select(5), .width(32)) multiplexer_1 (
    .in0(x0q), .in1(x1q), .in2(x2q), .in3(x3q), .in4(x4q), .in5(x5q), .in6(x6q), .in7(x7q), .in8(x8q),
    .in9(x9q), .in10(x10q), .in11(x11q), .in12(x12q), .in13(x13q), .in14(x14q), .in15(x15q), .in16(x16q),
    .in17(x17q), .in18(x18q), .in19(x19q), .in20(x20q), .in21(x21q), .in22(x22q), .in23(x23q), .in24(x24q),
    .in25(x25q), .in26(x26q), .in27(x27q), .in28(x28q), .in29(x29q), .in30(x30q), .in31(x31q_t), .out(rs1),
    .sel(rsi1));
  Multiplexer #(.select(5), .width(32)) multiplexer_2 (
    .in0(x0q), .in1(x1q), .in2(x2q), .in3(x3q), .in4(x4q), .in5(x5q), .in6(x6q), .in7(x7q), .in8(x8q),
    .in9(x9q), .in10(x10q), .in11(x11q), .in12(x12q), .in13(x13q), .in14(x14q), .in15(x15q), .in16(x16q),
    .in17(x17q), .in18(x18q), .in19(x19q), .in20(x20q), .in21(x21q), .in22(x22q), .in23(x23q), .in24(x24q),
    .in25(x25q), .in26(x26q), .in27(x27q), .in28(x28q), .in29(x29q), .in30(x30q), .in31(x31q_t), .out(rs2),
    .sel(rsi2));

  // Other names for the same wires on the sheet: Clk_t = clk; rdi_t[4:0] = rdi; rs1_t[31:0] = rs1; rs2_t[31:0] = rs2;
  //   rsi1_t[4:0] = rsi1; rsi2_t[4:0] = rsi2; WriteEnable = wena

  // Notes on the sheet:
  //   add rd, rs1,rs2
endmodule

module ISplitter (
  input  [31:0] Instruction,
  output [6:0] OpCode,
  output [4:0] rd,
  output [2:0] funct3,
  output [4:0] rs1,
  output [11:0] imm11_0
);


  assign funct3 = Instruction[14:12];
  assign imm11_0 = Instruction[31:20];
  assign OpCode = Instruction[6:0];
  assign rd = Instruction[11:7];
  assign rs1 = Instruction[19:15];
endmodule

module SSplitter (
  input  [31:0] Instruction,
  output [6:0] OpCode,
  output [4:0] imm4_0,
  output [2:0] funct3,
  output [4:0] rs1,
  output [4:0] rs2,
  output [6:0] imm11_5
);


  assign funct3 = Instruction[14:12];
  assign imm4_0 = Instruction[11:7];
  assign imm11_5 = Instruction[31:25];
  assign OpCode = Instruction[6:0];
  assign rs1 = Instruction[19:15];
  assign rs2 = Instruction[24:20];
endmodule

module BSplitter (
  input  [31:0] Instruction,
  output [6:0] OpCode,
  output imm11,
  output [3:0] imm4_1,
  output [2:0] funct3,
  output [4:0] rs1,
  output [4:0] rs2,
  output [5:0] imm10_5,
  output imm12
);


  assign funct3 = Instruction[14:12];
  assign imm4_1 = Instruction[11:8];
  assign imm10_5 = Instruction[30:25];
  assign imm11 = Instruction[7];
  assign imm12 = Instruction[31];
  assign OpCode = Instruction[6:0];
  assign rs1 = Instruction[19:15];
  assign rs2 = Instruction[24:20];
endmodule

module USplitter (
  input  [31:0] Instruction,
  output [6:0] OpCode,
  output [4:0] rd,
  output [19:0] imm31_12
);


  assign imm31_12 = Instruction[31:12];
  assign OpCode = Instruction[6:0];
  assign rd = Instruction[11:7];
endmodule

module JSplitter (
  input  [31:0] Instruction,
  output [6:0] OpCode,
  output [4:0] rd,
  output [7:0] imm19_12,
  output imm11,
  output [9:0] imm10_1,
  output imm20
);


  assign imm10_1 = Instruction[30:21];
  assign imm11 = Instruction[20];
  assign imm19_12 = Instruction[19:12];
  assign imm20 = Instruction[31];
  assign OpCode = Instruction[6:0];
  assign rd = Instruction[11:7];
endmodule

module RSplitter (
  input  [31:0] Instruction,
  output [6:0] OpCode,
  output [4:0] rd,
  output [2:0] funct3,
  output [4:0] rs1,
  output [4:0] rs2,
  output [6:0] funct7
);


  assign funct3 = Instruction[14:12];
  assign funct7 = Instruction[31:25];
  assign OpCode = Instruction[6:0];
  assign rd = Instruction[11:7];
  assign rs1 = Instruction[19:15];
  assign rs2 = Instruction[24:20];
endmodule

module ImmidiateGenerator (
  input  [31:0] Instruction,
  input  [2:0] Sel,
  output [31:0] imm31_0
);

  wire imm11_t, imm12, imm20;
  wire [3:0] imm4_1t;
  wire [4:0] ssplitter_1_imm4_0;
  wire [5:0] imm10_5t;
  wire [6:0] ssplitter_1_imm11_5;
  wire [7:0] imm19_12;
  wire [9:0] imm10_1t;
  wire [11:0] isplitter_1_imm11_0;
  wire [31:0] BOut_t, IOut_t, JOut_t, SOut_t;
  wire [31:12] UOut_t;

  ISplitter isplitter_1 (.Instruction(Instruction), .imm11_0(isplitter_1_imm11_0));  // open: OpCode, rd, funct3, rs1
  SSplitter ssplitter_1 (
    .Instruction(Instruction), .imm11_5(ssplitter_1_imm11_5), .imm4_0(ssplitter_1_imm4_0));  // open: OpCode, rs1, rs2, funct3
  BSplitter bsplitter_1 (
    .Instruction(Instruction), .imm10_5(imm10_5t), .imm4_1(imm4_1t), .imm12(imm12), .imm11(imm11_t));  // open: OpCode, rs1, rs2, funct3
  JSplitter jsplitter_1 (
    .Instruction(Instruction), .imm19_12(imm19_12), .imm10_1(imm10_1t), .imm11(imm11_t), .imm20(imm20));  // open: OpCode, rd
  USplitter usplitter_1 (.Instruction(Instruction), .imm31_12(UOut_t));  // open: OpCode, rd
  assign IOut_t = {{20{isplitter_1_imm11_0[11]}}, isplitter_1_imm11_0};  // Bit_Extender bit_extender_1
  assign SOut_t = {{20{ssplitter_1_imm11_5[6]}}, {ssplitter_1_imm11_5, ssplitter_1_imm4_0}};  // Bit_Extender bit_extender_2
  assign BOut_t = {{19{imm12}}, {imm12, imm11_t, imm10_5t, imm4_1t, 1'b0}};  // Bit_Extender bit_extender_3
  assign JOut_t = {{11{imm20}}, {imm20, imm19_12, imm11_t, imm10_1t, 1'b0}};  // Bit_Extender bit_extender_4
  Multiplexer #(.select(3), .width(32)) multiplexer_1 (
    .in0(IOut_t), .in1(SOut_t), .in2(BOut_t), .in3(JOut_t), .in4({UOut_t, {12{1'b0}}}), .out(imm31_0),
    .sel(Sel));  // open: in5, in6, in7

  // Other names for the same wires on the sheet: Ins_t[31:0] = Instruction; Sel_t[2:0] = Sel
endmodule

module Brancher (
  input  [31:0] dataA,
  input  [31:0] dataB,
  input  brUn,
  output brLt,
  output beEq
);

  wire comparator_1_lt, comparator_2_lt;

  Comparator #(.width(32)) comparator_1 (.a(dataA), .b(dataB), .eq(beEq), .lt(comparator_1_lt));  // open: gt
  Comparator #(.mode("unsigned"), .width(32)) comparator_2 (
    .a(dataA), .b(dataB), .lt(comparator_2_lt));  // open: gt, eq
  Multiplexer multiplexer_1 (.in0(comparator_1_lt), .in1(comparator_2_lt), .out(brLt), .sel(brUn));

  // Other names for the same wires on the sheet: brEq_t = beEq; brLt_t = brLt; brUn_t = brUn; dataA_t[31:0] = dataA;
  //   dataB_t[31:0] = dataB
endmodule

module DesignDataPath (
  input  Rest
);

  wire alu_1_zf, and_1_out, branch, bsel, clk, regwena, wbsel, wm;
  wire [2:0] immsel, lsel;
  wire [3:0] alusel;
  wire [7:0] bitselector_1_out, multiplexer_1_out, pcregister_1_outpc;
  wire [31:0] adder_1_out, alu_1_datad, aluctl_1_datab, bit_extender_1_out, dataD, datars2, immgen_1_imm31_0,
       ins, multiplexer_2_out, registerfile_1_rs1, shifter_1_out;

  Clock clock_1 (.out(clk));
  Multiplexer #(.width(8)) multiplexer_1 (
    .in0(bitselector_1_out), .in1({8{1'b0}}), .out(multiplexer_1_out), .sel(Rest));
  PcRegister pcregister_1 (.in_1(multiplexer_1_out), .CLK(clk), .OutPC(pcregister_1_outpc));
  ROM #(.dataWidth(32)) rom_1 (.addr(pcregister_1_outpc), .data(ins));
  assign bit_extender_1_out = {{24{pcregister_1_outpc[7]}}, pcregister_1_outpc};  // Bit_Extender bit_extender_1
  BitSelector #(.group(8), .width(32)) bitselector_1 (.in(adder_1_out), .out(bitselector_1_out), .sel(2'b00));
  ControlLogic controllogic_1 (
    .Instruction(ins), .immsel(immsel), .bsel(bsel), .lsel(lsel), .wbsel(wbsel), .branch(branch), .wm(wm),
    .RegWE(regwena), .AluSelect(alusel));
  RegisterFile registerfile_1 (
    .rd_Value(dataD), .wena(regwena), .clk(clk), .rsi1(ins[19:15]), .rsi2(ins[24:20]), .rdi(ins[11:7]),
    .rs1(registerfile_1_rs1), .rs2(datars2));
  ImmGen immgen_1 (.Instruction(ins), .Sel(immsel), .imm31_0(immgen_1_imm31_0));
  Shifter #(.shift("lr"), .width(32)) shifter_1 (.in(immgen_1_imm31_0), .\dist (5'b00010), .out(shifter_1_out));
  ALUctl aluctl_1 (.rs2(datars2), .imm31_0(immgen_1_imm31_0), .bsel(bsel), .dataB(aluctl_1_datab));
  Multiplexer #(.width(32)) multiplexer_2 (.in0(32'h1), .in1(shifter_1_out), .out(multiplexer_2_out), .sel(and_1_out));
  and and_1 (and_1_out, branch, alu_1_zf);
  Adder #(.width(32)) adder_1 (.a(bit_extender_1_out), .b(multiplexer_2_out), .out(adder_1_out));  // open: cin, cout
  ALU alu_1 (.Selector(alusel), .dataA(registerfile_1_rs1), .dataB(aluctl_1_datab), .dataD(alu_1_datad), .zf(alu_1_zf));
  Memory memory_1 (
    .dataA(alu_1_datad), .datars2(datars2), .wm(wm), .regw(regwena), .clk(clk), .lsel(lsel), .wbsel(wbsel),
    .dataD(dataD));

  // Other names for the same wires on the sheet: rdi[4:0] = ins[11:7]; rs1[4:0] = ins[19:15]; rs2[4:0] = ins[24:20]

  // Notes on the sheet:
  //   محمد حسین اسحاقی
  //   محمد یاسین فیروزی
  //   ابوالفضل رنگ آور
  //   امیر مهدی جعفری
  //   add x2 , x3 , x4
  //   sub x2 , x3 , x4
  //   or x2 , x3 , x4
  //   and x2 , x3 , x4
  //   پردازنده 32 بیتی RISCV 
  //   402405003
  //   402405032
  //   402405014
  //   402405008
  //   دستورات ابتدایی
  //   0x00418133
  //   0x40418133
  //   0x0041e133
  //   0x0041f133
  //   xor x2, x3, x4
  //   sll x2, x3, x4
  //   slt x2, x3, x4
  //   0x0041c133
  //   0x00419133
  //   0x0041a133
  //   contents of rom_1 (hex, n*v repeats v):
  //   a00093 900113 110a63 102023 a00193 118663 c00213 100393 100293
endmodule

module ControlLogic (
  input  [31:0] Instruction,
  output [3:0] AluSelect,
  output RegWE,
  output [2:0] immsel,
  output bsel,
  output wbsel,
  output [2:0] lsel,
  output branch,
  output wm
);

  ROM #(.addrWidth(9), .dataWidth(15)) rom_1 (
    .addr({Instruction[30], Instruction[14:12], Instruction[6:2]}),
    .data({branch, wm, lsel, wbsel, AluSelect, RegWE, immsel, bsel}));

  // Other names for the same wires on the sheet: i2_t = Instruction[2]; i3_t = Instruction[3]; i4_t = Instruction[4];
  //   i5_t = Instruction[5]; i6_t = Instruction[6]; i12_t = Instruction[12]; i13_t = Instruction[13];
  //   i14_t = Instruction[14]; i30_t = Instruction[30]; bsel_t = bsel; RegWE_t = RegWE; wbsel_t = wbsel; wm_t = wm;
  //   branch_t = branch; as0_t = AluSelect[0]; as1_t = AluSelect[1]; as2_t = AluSelect[2]; as3_t = AluSelect[3];
  //   is0_t = immsel[0]; is1_t = immsel[1]; is2_t = immsel[2]; lsel0_t = lsel[0]; lsel1_t = lsel[1];
  //   lsel2_t = lsel[2]

  // Notes on the sheet:
  //   contents of rom_1 (hex, n*v repeats v):
  //   11 0 0 0 211 7*0 210 11*0 4104 7*0 411 0 0 0 231 7*0 230 19*0 811 0 0 0 251 0 0 0 2005 0 0 0 250
  //   23*0 271 7*0 270 19*0 1011 0 0 0 291 7*0 290 19*0 1411 0 0 0 2b1 7*0 2b0 23*0 2d1 7*0 2d0 23*0 2f1
  //   7*0 2f0 31*0 310 151*0 3b1 7*0 3b0
endmodule

module PC_Reg (
  input  [31:0] InPc,
  input  CLK,
  output [31:0] OutPCPlus4,
  output [31:0] OutPC
);

  Register #(.width(32)) register_1 (.D(InPc), .en(1'b1), .clk(CLK), .Q(OutPC));  // open: clr
  Adder #(.width(32)) adder_1 (.a(OutPC), .b(32'h4), .out(OutPCPlus4));  // open: cin, cout

  // Other names for the same wires on the sheet: CLK_T = CLK; InPC_T[31:0] = InPc; OutPC_T[31:0] = OutPC;
  //   OutPCPlus4_T[31:0] = OutPCPlus4
endmodule

module ALUctl (
  input  [31:0] rs2,
  input  [31:0] imm31_0,
  input  bsel,
  output [31:0] dataB
);

  Multiplexer #(.width(32)) multiplexer_1 (.in0(rs2), .in1(imm31_0), .out(dataB), .sel(bsel));
endmodule

module LoadByte (
  input  [31:0] A_t,
  input  [31:0] Lw_t,
  output [31:0] lb_t,
  output [31:0] lbu_t
);

  wire [4:0] bitselector_1_out;
  wire [7:0] bitselector_2_out;
  wire [31:0] and_1_out, shifter_1_out, shifter_2_out, subtractor_1_out;

  assign and_1_out = A_t & 32'h3;  // AND_Gate and_1, 32 bits wide
  Subtractor #(.width(32)) subtractor_1 (.a(32'h3), .b(and_1_out), .out(subtractor_1_out));  // open: bin, bout
  Shifter #(.width(32)) shifter_1 (.in(subtractor_1_out), .\dist (5'b00011), .out(shifter_1_out));
  BitSelector #(.group(5), .width(32)) bitselector_1 (.in(shifter_1_out), .out(bitselector_1_out), .sel(3'b000));
  Shifter #(.shift("lr"), .width(32)) shifter_2 (.in(Lw_t), .\dist (bitselector_1_out), .out(shifter_2_out));
  BitSelector #(.group(8), .width(32)) bitselector_2 (.in(shifter_2_out), .out(bitselector_2_out), .sel(2'b00));
  assign lbu_t = 32'hff & shifter_2_out;  // AND_Gate and_2, 32 bits wide
  assign lb_t = {{24{bitselector_2_out[7]}}, bitselector_2_out};  // Bit_Extender bit_extender_1
endmodule

module LoadHalfword (
  input  [31:0] A_t,
  input  [31:0] Lw_t,
  output [31:0] lh_t,
  output [31:0] lhu_t
);

  wire bitselector_1_out, not_1_out;
  wire [15:0] bitselector_2_out;

  BitSelector #(.width(32)) bitselector_1 (.in(A_t), .out(bitselector_1_out), .sel(5'b00001));
  not not_1 (not_1_out, bitselector_1_out);
  BitSelector #(.group(16), .width(32)) bitselector_2 (.in(Lw_t), .out(bitselector_2_out), .sel(not_1_out));
  assign lh_t = {{16{bitselector_2_out[15]}}, bitselector_2_out};  // Bit_Extender bit_extender_1
  assign lhu_t = {{16{1'b0}}, bitselector_2_out};  // Bit_Extender bit_extender_2
endmodule

module Loadctl (
  input  [31:0] A,
  input  [31:0] lw,
  input  [2:0] lsel,
  input  wbsel,
  output [31:0] D
);

  wire [31:0] lb_t, lbu_t, lh_t, lhu_t, multiplexer_1_out;

  Multiplexer #(.select(3), .width(32)) multiplexer_1 (
    .in0(lb_t), .in1(lh_t), .in2(lw), .in3(lbu_t), .in4(lhu_t), .out(multiplexer_1_out), .sel(lsel));  // open: in5, in6, in7
  LoadHalfword loadhalfword_1 (.A_t(A), .Lw_t(lw), .lh_t(lh_t), .lhu_t(lhu_t));
  LoadByte loadbyte_1 (.A_t(A), .Lw_t(lw), .lb_t(lb_t), .lbu_t(lbu_t));
  Multiplexer #(.width(32)) multiplexer_2 (.in0(multiplexer_1_out), .in1(A), .out(D), .sel(wbsel));

  // Other names for the same wires on the sheet: A_t[31:0] = A; D_t[31:0] = D; lsel_t[2:0] = lsel; lw_t[31:0] = lw;
  //   wbsel_t = wbsel
endmodule

module Mem (
);

  wire clk;
  wire [1:0] undriven, undriven_2;
  wire [7:0] bitselector_1_out, bitselector_2_out, undriven_3, undriven_4;

  BitSelector #(.group(8), .width(32)) bitselector_1 (.out(bitselector_1_out), .sel(undriven));  // open: in
  BitSelector #(.group(8), .width(32)) bitselector_2 (.out(bitselector_2_out), .sel(undriven_2));  // open: in
  RAM #(.dataWidth(32)) ram_1 (.addr(undriven_3), .clk(clk));  // open: we, oe, din, dout
  RAM #(.dataWidth(32)) ram_2 (.addr(undriven_4), .clk(clk));  // open: we, oe, din, dout
endmodule

module Memory (
  input  [31:0] dataA,
  input  [31:0] datars2,
  input  wm,
  input  regw,
  input  clk,
  input  [2:0] lsel,
  input  wbsel,
  output [31:0] dataD
);

  wire [7:0] bitselector_1_out, shifter_1_out;
  wire [31:0] lw_t;

  BitSelector #(.group(8), .width(32)) bitselector_1 (.in(dataA), .out(bitselector_1_out), .sel(2'b00));
  Shifter #(.shift("lr")) shifter_1 (.in(bitselector_1_out), .\dist (3'b010), .out(shifter_1_out));
  RAM #(.dataWidth(32)) ram_1 (.addr(shifter_1_out), .we(wm), .oe(regw), .clk(clk), .din(datars2), .dout(lw_t));
  Loadctl loadctl_1 (.A(dataA), .lw(lw_t), .lsel(lsel), .wbsel(wbsel), .D(dataD));

  // Other names for the same wires on the sheet: rs2[31:0] = datars2
endmodule

module PcRegister (
  input  [7:0] in_1,
  input  CLK,
  output [7:0] OutPC
);

  Register register_1 (.D(in_1), .en(1'b1), .clk(CLK), .Q(OutPC));  // open: clr

  // Other names for the same wires on the sheet: CLK_T = CLK; InPC_T[7:0] = in_1
endmodule

module ImmGen (
  input  [31:0] Instruction,
  input  [2:0] Sel,
  output [31:0] imm31_0
);

  wire imm11_t, imm12, imm20;
  wire [3:0] imm4_1t;
  wire [4:0] ssplitter_1_imm4_0;
  wire [5:0] imm10_5t;
  wire [6:0] ssplitter_1_imm11_5;
  wire [7:0] imm19_12;
  wire [9:0] imm10_1t;
  wire [11:0] isplitter_1_imm11_0;
  wire [31:0] BOut_t, IOut_t, JOut_t, SOut_t;
  wire [31:12] UOut_t;

  ISplitter isplitter_1 (.Instruction(Instruction), .imm11_0(isplitter_1_imm11_0));  // open: OpCode, rd, funct3, rs1
  SSplitter ssplitter_1 (
    .Instruction(Instruction), .imm11_5(ssplitter_1_imm11_5), .imm4_0(ssplitter_1_imm4_0));  // open: OpCode, rs1, rs2, funct3
  BSplitter bsplitter_1 (
    .Instruction(Instruction), .imm10_5(imm10_5t), .imm4_1(imm4_1t), .imm12(imm12), .imm11(imm11_t));  // open: OpCode, rs1, rs2, funct3
  JSplitter jsplitter_1 (
    .Instruction(Instruction), .imm19_12(imm19_12), .imm10_1(imm10_1t), .imm11(imm11_t), .imm20(imm20));  // open: OpCode, rd
  USplitter usplitter_1 (.Instruction(Instruction), .imm31_12(UOut_t));  // open: OpCode, rd
  assign IOut_t = {{20{isplitter_1_imm11_0[11]}}, isplitter_1_imm11_0};  // Bit_Extender bit_extender_1
  assign SOut_t = {{20{ssplitter_1_imm11_5[6]}}, {ssplitter_1_imm11_5, ssplitter_1_imm4_0}};  // Bit_Extender bit_extender_2
  assign BOut_t = {{19{imm12}}, {imm12, imm11_t, imm10_5t, imm4_1t, 1'b0}};  // Bit_Extender bit_extender_3
  assign JOut_t = {{11{imm20}}, {imm20, imm19_12, imm11_t, imm10_1t, 1'b0}};  // Bit_Extender bit_extender_4
  Multiplexer #(.select(3), .width(32)) multiplexer_1 (
    .in0(IOut_t), .in1(SOut_t), .in2(BOut_t), .in3(JOut_t), .in4({UOut_t, {12{1'b0}}}), .out(imm31_0),
    .sel(Sel));  // open: in5, in6, in7

  // Other names for the same wires on the sheet: Ins_t[31:0] = Instruction; Sel_t[2:0] = Sel
endmodule
