// Logisim project FISC_V.circ as structural Verilog: 13 circuits, main circuit main
module main (
  input  [31:0] InPc,
  input  CLK,
  output [31:0] OutPCPlus4,
  output [31:0] OutPC
);

  ISplitter isplitter_1 ();  // open: Instruction, OpCode, rd, funct3, rs1, imm11_0
  SSplitter ssplitter_1 ();  // open: Instruction, OpCode, imm4_0, funct3, rs1, rs2, imm11_5
  BSplitter bsplitter_1 ();  // open: Instruction, OpCode, imm11, imm4_1, funct3, rs1, rs2, imm10_5, imm12
  USplitter usplitter_1 ();  // open: Instruction, OpCode, rd, imm31_12
  JSplitter jsplitter_1 ();  // open: Instruction, OpCode, rd, imm19_12, imm11, imm10_1, imm20
  RSplitter rsplitter_1 ();  // open: Instruction, OpCode, rd, funct3, rs1, rs2, funct7
  Register #(.width(32)) register_1 (.D(InPc), .en(1'b1), .clk(CLK), .Q(OutPC));  // open: clr
  Adder #(.width(32)) adder_1 (.a(OutPC), .b(32'h4), .out(OutPCPlus4));  // open: cin, cout

  // Other names for the same wires on the sheet: CLK_T = CLK; InPC_T[31:0] = InPc; OutPC_T[31:0] = OutPC;
  //   OutPCPlus4_T[31:0] = OutPCPlus4
endmodule

module ALU (
  input  [31:0] dataA,
  input  [31:0] dataB,
  input  [3:0] Selector,
  output [31:0] dataD
);

  wire comparator_1_lt, comparator_2_lt;
  wire [31:0] addOut, andOut, orOut, sllOut, sltOut, sltuOut, sraOut, srlOut, subOut, xorOut;

  Adder #(.width(32)) adder_1 (.a(dataA), .b(dataB), .out(addOut));  // open: cin, cout
  Subtractor #(.width(32)) subtractor_1 (.a(dataA), .b(dataB), .out(subOut));  // open: bin, bout
  Shifter #(.width(32)) shifter_1 (.in(dataA), .\dist (dataB[4:0]), .out(sllOut));
  Comparator #(.width(32)) comparator_1 (.a(dataA), .b(dataB), .lt(comparator_1_lt));  // open: gt, eq
  Comparator #(.width(32), .mode("unsigned")) comparator_2 (
    .a(dataA), .b(dataB), .lt(comparator_2_lt));  // open: gt, eq
  assign xorOut = dataA ^ dataB;  // XOR_Gate xor_1, 32 bits wide
  Shifter #(.width(32), .shift("lr")) shifter_2 (.in(dataA), .\dist (dataB[4:0]), .out(srlOut));
  Shifter #(.width(32), .shift("ar")) shifter_3 (.in(dataA), .\dist (dataB[4:0]), .out(sraOut));
  assign orOut = dataA | dataB;  // OR_Gate or_1, 32 bits wide
  assign andOut = dataA & dataB;  // AND_Gate and_1, 32 bits wide
  assign sltOut = {{31{comparator_1_lt}}, comparator_1_lt};  // Bit_Extender bit_extender_1
  assign sltuOut = {{31{comparator_2_lt}}, comparator_2_lt};  // Bit_Extender bit_extender_2
  Multiplexer #(.select(4), .width(32), .enable("false")) multiplexer_1 (
    .in0(addOut), .in1(sllOut), .in2(sltOut), .in3(sltuOut), .in4(xorOut), .in5(srlOut), .in6(orOut),
    .in7(andOut), .in8(subOut), .in13(sraOut), .out(dataD), .sel(Selector));  // open: in9, in10, in11, in12, in14, in15

  // Other names for the same wires on the sheet: dataBL5[4:0] = dataB[4:0]; dataD_T[31:0] = dataD;
  //   Selector_T[3:0] = Selector

  // Notes on the sheet:
  //   0000 add
  //   1000 sub
  //   دستورات مربوط به ALU
  //   0001 sll - Shift Left Logical
  //   0010 slt - Set Less Than
  //   0011 sltu - Set Less Than Unsigned
  //   0100 xor - eXclusive OR
  //   0101 srl - Shift Right Logical
  //   1101 sra - Shift Right Arithmetic
  //   0110 or - Logical OR
  //   0111 and - Logical AND
endmodule

module RegisterFile (
  input  [4:0] rsi1,
  input  [4:0] rsi2,
  input  [4:0] rdi,
  input  Write_Enable,
  input  in_5,
  input  [31:0] rd_Value,
  output [31:0] rs1,
  output [31:0] rs2
);

  wire x0we_t, x1we_t, x2we_t, x3we_t, x4we_t, x5we_t, x6we_t, x7we_t, x8we_t, x9we_t, x10we_t, x11we_t,
       x12we_t, x13we_t, x14we_t, x15we_t, x16we_t, x17we_t, x18we_t, x19we_t, x20we_t, x21we_t, x22we_t,
       x23we_t, x24we_t, x25we_t, x26we_t, x27we_t, x28we_t, x29we_t, x30we_t, x31we_t;
  wire [31:0] x0q, x1q, x2q, x3q, x4q, x5q, x6q, x7q, x8q, x9q, x10q, x11q, x12q, x13q, x14q, x15q, x16q,
       x17q, x18q, x19q, x20q, x21q, x22q, x23q, x24q, x25q, x26q, x27q, x28q, x29q, x30q, x31q;

  Demultiplexer #(.select(5), .enable("false")) demultiplexer_1 (
    .out0(x0we_t), .out1(x1we_t), .out2(x2we_t), .out3(x3we_t), .out4(x4we_t), .out5(x5we_t), .out6(x6we_t),
    .out7(x7we_t), .out8(x8we_t), .out9(x9we_t), .out10(x10we_t), .out11(x11we_t), .out12(x12we_t),
    .out13(x13we_t), .out14(x14we_t), .out15(x15we_t), .out16(x16we_t), .out17(x17we_t), .out18(x18we_t),
    .out19(x19we_t), .out20(x20we_t), .out21(x21we_t), .out22(x22we_t), .out23(x23we_t), .out24(x24we_t),
    .out25(x25we_t), .out26(x26we_t), .out27(x27we_t), .out28(x28we_t), .out29(x29we_t), .out30(x30we_t),
    .out31(x31we_t), .in(Write_Enable), .sel(rdi));
  Register #(.width(32)) x0 (.D(rd_Value), .en(x0we_t), .clk(in_5), .Q(x0q));  // open: clr
  Register #(.width(32)) x4 (.D(rd_Value), .en(x4we_t), .clk(in_5), .Q(x4q));  // open: clr
  Register #(.width(32)) x8 (.D(rd_Value), .en(x8we_t), .clk(in_5), .Q(x8q));  // open: clr
  Register #(.width(32)) x12 (.D(rd_Value), .en(x12we_t), .clk(in_5), .Q(x12q));  // open: clr
  Register #(.width(32)) x16 (.D(rd_Value), .en(x16we_t), .clk(in_5), .Q(x16q));  // open: clr
  Register #(.width(32)) x20 (.D(rd_Value), .en(x20we_t), .clk(in_5), .Q(x20q));  // open: clr
  Register #(.width(32)) x24 (.D(rd_Value), .en(x24we_t), .clk(in_5), .Q(x24q));  // open: clr
  Register #(.width(32)) x28 (.D(rd_Value), .en(x28we_t), .clk(in_5), .Q(x28q));  // open: clr
  Register #(.width(32)) x1 (.D(rd_Value), .en(x1we_t), .clk(in_5), .Q(x1q));  // open: clr
  Register #(.width(32)) x5 (.D(rd_Value), .en(x5we_t), .clk(in_5), .Q(x5q));  // open: clr
  Register #(.width(32)) x9 (.D(rd_Value), .en(x9we_t), .clk(in_5), .Q(x9q));  // open: clr
  Register #(.width(32)) x13 (.D(rd_Value), .en(x13we_t), .clk(in_5), .Q(x13q));  // open: clr
  Register #(.width(32)) x17 (.D(rd_Value), .en(x17we_t), .clk(in_5), .Q(x17q));  // open: clr
  Register #(.width(32)) x21 (.D(rd_Value), .en(x21we_t), .clk(in_5), .Q(x21q));  // open: clr
  Register #(.width(32)) x25 (.D(rd_Value), .en(x25we_t), .clk(in_5), .Q(x25q));  // open: clr
  Register #(.width(32)) x29 (.D(rd_Value), .en(x29we_t), .clk(in_5), .Q(x29q));  // open: clr
  Register #(.width(32)) x2 (.D(rd_Value), .en(x2we_t), .clk(in_5), .Q(x2q));  // open: clr
  Register #(.width(32)) x6 (.D(rd_Value), .en(x6we_t), .clk(in_5), .Q(x6q));  // open: clr
  Register #(.width(32)) x10 (.D(rd_Value), .en(x10we_t), .clk(in_5), .Q(x10q));  // open: clr
  Register #(.width(32)) x14 (.D(rd_Value), .en(x14we_t), .clk(in_5), .Q(x14q));  // open: clr
  Register #(.width(32)) x18 (.D(rd_Value), .en(x18we_t), .clk(in_5), .Q(x18q));  // open: clr
  Register #(.width(32)) x22 (.D(rd_Value), .en(x22we_t), .clk(in_5), .Q(x22q));  // open: clr
  Register #(.width(32)) x26 (.D(rd_Value), .en(x26we_t), .clk(in_5), .Q(x26q));  // open: clr
  Register #(.width(32)) x30 (.D(rd_Value), .en(x30we_t), .clk(in_5), .Q(x30q));  // open: clr
  Register #(.width(32)) x3 (.D(rd_Value), .en(x3we_t), .clk(in_5), .Q(x3q));  // open: clr
  Register #(.width(32)) x7 (.D(rd_Value), .en(x7we_t), .clk(in_5), .Q(x7q));  // open: clr
  Register #(.width(32)) x11 (.D(rd_Value), .en(x11we_t), .clk(in_5), .Q(x11q));  // open: clr
  Register #(.width(32)) x15 (.D(rd_Value), .en(x15we_t), .clk(in_5), .Q(x15q));  // open: clr
  Register #(.width(32)) x19 (.D(rd_Value), .en(x19we_t), .clk(in_5), .Q(x19q));  // open: clr
  Register #(.width(32)) x23 (.D(rd_Value), .en(x23we_t), .clk(in_5), .Q(x23q));  // open: clr
  Register #(.width(32)) x27 (.D(rd_Value), .en(x27we_t), .clk(in_5), .Q(x27q));  // open: clr
  Register #(.width(32)) register_1 (.D(rd_Value), .en(x31we_t), .clk(in_5), .Q(x31q));  // open: clr
  Multiplexer #(.select(5), .width(32), .enable("false")) multiplexer_1 (
    .in0(x0q), .in1(x1q), .in2(x2q), .in3(x3q), .in4(x4q), .in5(x5q), .in6(x6q), .in7(x7q), .in8(x8q),
    .in9(x9q), .in10(x10q), .in11(x11q), .in12(x12q), .in13(x13q), .in14(x14q), .in15(x15q), .in16(x16q),
    .in17(x17q), .in18(x18q), .in19(x19q), .in20(x20q), .in21(x21q), .in22(x22q), .in23(x23q), .in24(x24q),
    .in25(x25q), .in26(x26q), .in27(x27q), .in28(x28q), .in29(x29q), .in30(x30q), .in31(x31q), .out(rs1),
    .sel(rsi1));
  Multiplexer #(.select(5), .width(32), .enable("false")) multiplexer_2 (
    .in0(x0q), .in1(x1q), .in2(x2q), .in3(x3q), .in4(x4q), .in5(x5q), .in6(x6q), .in7(x7q), .in8(x8q),
    .in9(x9q), .in10(x10q), .in11(x11q), .in12(x12q), .in13(x13q), .in14(x14q), .in15(x15q), .in16(x16q),
    .in17(x17q), .in18(x18q), .in19(x19q), .in20(x20q), .in21(x21q), .in22(x22q), .in23(x23q), .in24(x24q),
    .in25(x25q), .in26(x26q), .in27(x27q), .in28(x28q), .in29(x29q), .in30(x30q), .in31(x31q), .out(rs2),
    .sel(rsi2));

  // Other names for the same wires on the sheet: Clk_t = in_5; rdi_t[4:0] = rdi; rs1_t[31:0] = rs1; rs2_t[31:0] = rs2;
  //   rsi1_t[4:0] = rsi1; rsi2_t[4:0] = rsi2; WriteEnable = Write_Enable

  // Notes on the sheet:
  //   add rd, rs1,rs2
endmodule

module ISplitter (
  input  [31:0] Instruction,
  output [6:0] OpCode,
  output [4:0] rd,
  output [2:0] funct3,
  output [4:0] rs1,
  output [11:0] imm11_0
);


  assign funct3 = Instruction[14:12];
  assign imm11_0 = Instruction[31:20];
  assign OpCode = Instruction[6:0];
  assign rd = Instruction[11:7];
  assign rs1 = Instruction[19:15];
endmodule

module SSplitter (
  input  [31:0] Instruction,
  output [6:0] OpCode,
  output [4:0] imm4_0,
  output [2:0] funct3,
  output [4:0] rs1,
  output [4:0] rs2,
  output [6:0] imm11_5
);


  assign funct3 = Instruction[14:12];
  assign imm4_0 = Instruction[11:7];
  assign imm11_5 = Instruction[31:25];
  assign OpCode = Instruction[6:0];
  assign rs1 = Instruction[19:15];
  assign rs2 = Instruction[24:20];
endmodule

module BSplitter (
  input  [31:0] Instruction,
  output [6:0] OpCode,
  output imm11,
  output [3:0] imm4_1,
  output [2:0] funct3,
  output [4:0] rs1,
  output [4:0] rs2,
  output [5:0] imm10_5,
  output imm12
);


  assign funct3 = Instruction[14:12];
  assign imm4_1 = Instruction[11:8];
  assign imm10_5 = Instruction[30:25];
  assign imm11 = Instruction[7];
  assign imm12 = Instruction[31];
  assign OpCode = Instruction[6:0];
  assign rs1 = Instruction[19:15];
  assign rs2 = Instruction[24:20];
endmodule

module USplitter (
  input  [31:0] Instruction,
  output [6:0] OpCode,
  output [4:0] rd,
  output [19:0] imm31_12
);


  assign imm31_12 = Instruction[31:12];
  assign OpCode = Instruction[6:0];
  assign rd = Instruction[11:7];
endmodule

module JSplitter (
  input  [31:0] Instruction,
  output [6:0] OpCode,
  output [4:0] rd,
  output [7:0] imm19_12,
  output imm11,
  output [9:0] imm10_1,
  output imm20
);


  assign imm10_1 = Instruction[30:21];
  assign imm11 = Instruction[20];
  assign imm19_12 = Instruction[19:12];
  assign imm20 = Instruction[31];
  assign OpCode = Instruction[6:0];
  assign rd = Instruction[11:7];
endmodule

module RSplitter (
  input  [31:0] Instruction,
  output [6:0] OpCode,
  output [4:0] rd,
  output [2:0] funct3,
  output [4:0] rs1,
  output [4:0] rs2,
  output [6:0] funct7
);


  assign funct3 = Instruction[14:12];
  assign funct7 = Instruction[31:25];
  assign OpCode = Instruction[6:0];
  assign rd = Instruction[11:7];
  assign rs1 = Instruction[19:15];
  assign rs2 = Instruction[24:20];
endmodule

module ImmidiateGenerator (
  input  [31:0] Instruction,
  input  [2:0] Sel,
  output [31:0] imm31_0
);

  wire imm11_t, imm12, imm20;
  wire [3:0] imm4_1t;
  wire [4:0] ssplitter_1_imm4_0;
  wire [5:0] imm10_5t;
  wire [6:0] ssplitter_1_imm11_5;
  wire [7:0] imm19_12;
  wire [9:0] imm10_1t;
  wire [11:0] isplitter_1_imm11_0;
  wire [31:0] BOut_t, IOut_t, JOut_t, SOut_t;
  wire [31:12] UOut_t;

  ISplitter isplitter_1 (.Instruction(Instruction), .imm11_0(isplitter_1_imm11_0));  // open: OpCode, rd, funct3, rs1
  SSplitter ssplitter_1 (
    .Instruction(Instruction), .imm4_0(ssplitter_1_imm4_0), .imm11_5(ssplitter_1_imm11_5));  // open: OpCode, funct3, rs1, rs2
  BSplitter bsplitter_1 (
    .Instruction(Instruction), .imm11(imm11_t), .imm4_1(imm4_1t), .imm10_5(imm10_5t), .imm12(imm12));  // open: OpCode, funct3, rs1, rs2
  JSplitter jsplitter_1 (
    .Instruction(Instruction), .imm19_12(imm19_12), .imm11(imm11_t), .imm10_1(imm10_1t), .imm20(imm20));  // open: OpCode, rd
  USplitter usplitter_1 (.Instruction(Instruction), .imm31_12(UOut_t));  // open: OpCode, rd
  assign IOut_t = {{20{isplitter_1_imm11_0[11]}}, isplitter_1_imm11_0};  // Bit_Extender bit_extender_1
  assign SOut_t = {{20{ssplitter_1_imm11_5[6]}}, {ssplitter_1_imm11_5, ssplitter_1_imm4_0}};  // Bit_Extender bit_extender_2
  assign BOut_t = {{19{imm12}}, {imm12, imm11_t, imm10_5t, imm4_1t, 1'b0}};  // Bit_Extender bit_extender_3
  assign JOut_t = {{11{imm20}}, {imm20, imm19_12, imm11_t, imm10_1t, 1'b0}};  // Bit_Extender bit_extender_4
  Multiplexer #(.select(3), .width(32), .enable("false")) multiplexer_1 (
    .in0(IOut_t), .in1(SOut_t), .in2(BOut_t), .in3(JOut_t), .in4({UOut_t, {12{1'b0}}}), .out(imm31_0),
    .sel(Sel));  // open: in5, in6, in7

  // Other names for the same wires on the sheet: Ins_t[31:0] = Instruction; Sel_t[2:0] = Sel
endmodule

module Brancher (
  input  [31:0] dataA,
  input  [31:0] dataB,
  input  brUn,
  output brLt,
  output beEq
);

  wire comparator_1_lt, comparator_2_lt;

  Comparator #(.width(32)) comparator_1 (.a(dataA), .b(dataB), .eq(beEq), .lt(comparator_1_lt));  // open: gt
  Comparator #(.width(32), .mode("unsigned")) comparator_2 (
    .a(dataA), .b(dataB), .lt(comparator_2_lt));  // open: gt, eq
  Multiplexer #(.enable("false")) multiplexer_1 (.in0(comparator_1_lt), .in1(comparator_2_lt), .out(brLt), .sel(brUn));

  // Other names for the same wires on the sheet: brEq_t = beEq; brLt_t = brLt; brUn_t = brUn; dataA_t[31:0] = dataA;
  //   dataB_t[31:0] = dataB
endmodule

module DesignDataPath (
  input  [31:0] Instruction,
  output [31:0] Result
);

  wire clock_1_out, undriven;
  wire [3:0] undriven_2;
  wire [4:0] rsplitter_1_rd, rsplitter_1_rs1, rsplitter_1_rs2;
  wire [31:0] registerfile_1_rs1, registerfile_1_rs2;

  Clock clock_1 (.out(clock_1_out));
  RSplitter rsplitter_1 (
    .Instruction(Instruction), .rd(rsplitter_1_rd), .rs1(rsplitter_1_rs1), .rs2(rsplitter_1_rs2));  // open: OpCode, funct3, funct7
  ControlLogic controllogic_1 (.Instruction(Instruction), .AluSelect(undriven_2), .RegWE(undriven));
  RegisterFile registerfile_1 (
    .rsi1(rsplitter_1_rs1), .rsi2(rsplitter_1_rs2), .rdi(rsplitter_1_rd), .Write_Enable(undriven),
    .rd_Value(Result), .rs1(registerfile_1_rs1), .rs2(registerfile_1_rs2), .in_5(clock_1_out));
  ALU alu_1 (.dataA(registerfile_1_rs1), .dataB(registerfile_1_rs2), .Selector(undriven_2), .dataD(Result));

  // Notes on the sheet:
  //   add x2 , x3 , x4
  //   sub x2 , x3 , x4
  //   or x2 , x3 , x4
  //   and x2 , x3 , x4
  //   0x004118133
  //   0x404118133
  //   0x00411e133
  //   0x0041f133
endmodule

module ControlLogic (
  input  [3:0] AluSelect,
  input  RegWE,
  input  [31:0] Instruction
);

  wire add_t, or_t;

  and and_1 (add_t, ~Instruction[2], ~Instruction[3], Instruction[4], Instruction[5], ~Instruction[6], ~Instruction[12], ~Instruction[13], ~Instruction[14], ~Instruction[30]);  // AND_Gate
  and and_2 (AluSelect[3], ~Instruction[2], ~Instruction[3], Instruction[4], Instruction[5], ~Instruction[6], ~Instruction[12], ~Instruction[13], ~Instruction[14], Instruction[30]);  // AND_Gate
  and and_3 (or_t, ~Instruction[2], ~Instruction[3], Instruction[4], Instruction[5], ~Instruction[6], ~Instruction[12], Instruction[13], Instruction[14], ~Instruction[30]);  // AND_Gate
  and and_4 (AluSelect[0], ~Instruction[2], ~Instruction[3], Instruction[4], Instruction[5], ~Instruction[6], Instruction[12], Instruction[13], Instruction[14], ~Instruction[30]);  // AND_Gate
  or or_1 (AluSelect[2], or_t, AluSelect[0]);
  or or_2 (RegWE, add_t, AluSelect[3], AluSelect[0], or_t);

  assign AluSelect[1] = AluSelect[2];

  // Other names for the same wires on the sheet: and_t = AluSelect[0]; as0_t = AluSelect[0]; as1_t = AluSelect[2];
  //   as2_t = AluSelect[2]; as3_t = AluSelect[3]; sub_t = AluSelect[3]; i2_t = Instruction[2]; i3_t = Instruction[3];
  //   i4_t = Instruction[4]; i5_t = Instruction[5]; i6_t = Instruction[6]; i12_t = Instruction[12];
  //   i13_t = Instruction[13]; i14_t = Instruction[14]; i30_t = Instruction[30]
endmodule
