// Logisim project FISCProgramCounter.circ as structural Verilog: 1 circuit, main circuit main
module main (
  input  [31:0] inPC,
  input  CLK
);

  wire [31:0] OutPCPlus4, PcOut;

  Register #(.width(32)) register_1 (.D(inPC), .en(1'b1), .clk(CLK), .Q(PcOut));  // open: clr
  Adder #(.width(32)) adder_1 (.a(PcOut), .b(32'h4), .out(OutPCPlus4));  // open: cin, cout
  // Probe on OutPCPlus4
  // Probe on PcOut

  // Other names for the same wires on the sheet: CLK_T = CLK; inPC_T[31:0] = inPC
endmodule
