// Logisim project Processor.circ as structural Verilog: 23 circuits, main circuit Processor
// reg
module Processor (
  input  Reset,
  input  [3:0] Display_Address
);

  wire alu_1_is, alu_1_is_2, Clock, control_unit_1_isbeq, control_unit_1_isbgt, control_unit_1_iscall,
       control_unit_1_isimmediate, control_unit_1_isld, control_unit_1_isret, control_unit_1_isst,
       control_unit_1_isubranch, control_unit_1_iswb, data_lock_unit_1_data_lock_conflict,
       ex_ma_latch_1_out_16, ex_ma_latch_1_out_17, ex_ma_latch_1_out_18, ex_ma_latch_1_out_19,
       flags_1_flags_e, flags_1_flags_gt, isBranchTaken, isWb, of_ex_latch_1_out_27, of_ex_latch_1_out_28,
       of_ex_latch_1_out_29, of_ex_latch_1_out_30, of_ex_latch_1_out_31, of_ex_latch_1_out_32,
       of_ex_latch_1_out_33, of_ex_latch_1_out_34, or_1_out, RW__EX_op2, RW__MA_op2, RW__OF_op1, RW__OF_op2,
       Stall;
  wire [1:0] ma_rw_latch_1_out_15, RW_MA__EX_op1, RW_MA__EX_op2;
  wire [3:0] ma_rw_latch_1_out_14_2, multiplexer_8_out, multiplexer_11_out, multiplexer_14_out_2,
       multiplexer_14_out_3, \reg ;
  wire [12:0] control_unit_1_alusignals, of_ex_latch_1_out_26;
  wire [31:0] adder_1_out, adder_2_out, adder_3_out, alu_1_aluresult, aluResult, bit_extender_1_out,
       branchTarget, calculate_immediate_1_immx, data, EX_MA_Instruction, ex_ma_latch_1_out_12,
       ex_ma_latch_1_out_14, ex_ma_latch_1_out_15, IF_OF_Instruction, if_of_latch_1_out_8, MA_RW_Instruction,
       ma_rw_latch_1_out_11, ma_rw_latch_1_out_12, ma_rw_latch_1_out_13, ma_rw_latch_1_out_14,
       memory_unit_1_ldresult, multiplexer_1_out, multiplexer_2_out, multiplexer_3_out, multiplexer_4_out,
       multiplexer_7_out, multiplexer_9_out, multiplexer_10_out, multiplexer_12_out, multiplexer_14_out,
       OF_EX_Instruction, of_ex_latch_1_out_20, of_ex_latch_1_out_21, of_ex_latch_1_out_22,
       of_ex_latch_1_out_23, of_ex_latch_1_out_24, of_ex_latch_1_out_25, PC_q, register_file_1_displayd,
       register_file_1_readd1, register_file_1_readd2, rom_1_data, shifter_1_out;

  IF_OF_Latch if_of_latch_1 (
    .in_4(Clock), .in_2(PC_q),
    .in_3({multiplexer_14_out[31:26], multiplexer_14_out_3, multiplexer_14_out_2, multiplexer_14_out[17:0]}),
    .out_8(if_of_latch_1_out_8), .in_5(Reset), .out_6(IF_OF_Instruction), .Stall(Stall));  // open: out_7
  OF_EX_Latch of_ex_latch_1 (
    .in_17(Clock), .in_4(if_of_latch_1_out_8), .in_5(adder_3_out), .in_6(multiplexer_7_out),
    .in_7(multiplexer_12_out), .in_8(multiplexer_9_out),
    .isRet({multiplexer_14_out[31:26], multiplexer_14_out_3, multiplexer_14_out_2, multiplexer_14_out[17:0]}),
    .in_1(control_unit_1_isret), .in_2(control_unit_1_alusignals), .in_10(control_unit_1_isbeq),
    .isBgt(control_unit_1_isbgt), .isUBranch(control_unit_1_isubranch), .isLd(control_unit_1_isld),
    .isSt(control_unit_1_isst), .in_15(control_unit_1_iscall), .in_16(control_unit_1_iswb),
    .out_20(of_ex_latch_1_out_20), .out_21(of_ex_latch_1_out_21), .out_22(of_ex_latch_1_out_22),
    .out_23(of_ex_latch_1_out_23), .out_24(of_ex_latch_1_out_24), .out_25(of_ex_latch_1_out_25),
    .out_27(of_ex_latch_1_out_27), .out_26(of_ex_latch_1_out_26), .out_28(of_ex_latch_1_out_28),
    .out_29(of_ex_latch_1_out_29), .out_30(of_ex_latch_1_out_30), .out_31(of_ex_latch_1_out_31),
    .out_32(of_ex_latch_1_out_32), .out_33(of_ex_latch_1_out_33), .out_34(of_ex_latch_1_out_34),
    .in_18(Reset), .out_19(OF_EX_Instruction), .Bubble(or_1_out));
  EX_MA_Latch ex_ma_latch_1 (
    .in_9(Clock), .in_5(of_ex_latch_1_out_20), .in_6(alu_1_aluresult), .in_7(multiplexer_3_out),
    .in_8(of_ex_latch_1_out_25), .isLd(of_ex_latch_1_out_31), .isSt(of_ex_latch_1_out_32),
    .isCall(of_ex_latch_1_out_33), .isWb(of_ex_latch_1_out_34), .out_12(ex_ma_latch_1_out_12),
    .out_13(aluResult), .out_14(ex_ma_latch_1_out_14), .out_15(ex_ma_latch_1_out_15),
    .out_16(ex_ma_latch_1_out_16), .out_17(ex_ma_latch_1_out_17), .out_18(ex_ma_latch_1_out_18),
    .out_19(ex_ma_latch_1_out_19), .in_10(Reset), .out_11(EX_MA_Instruction));
  MA_RW_Latch ma_rw_latch_1 (
    .in_8(Clock), .in_4(ex_ma_latch_1_out_12), .in_5(memory_unit_1_ldresult), .in_6(aluResult),
    .in_7(ex_ma_latch_1_out_15), .isLd(ex_ma_latch_1_out_16), .isCall(ex_ma_latch_1_out_18),
    .isWb(ex_ma_latch_1_out_19), .out_11(ma_rw_latch_1_out_11), .out_12(ma_rw_latch_1_out_12),
    .out_13(ma_rw_latch_1_out_13),
    .out_14({ma_rw_latch_1_out_14[31:26], ma_rw_latch_1_out_14_2, ma_rw_latch_1_out_14[21:0]}),
    .out_15(ma_rw_latch_1_out_15[0]), .out_16(ma_rw_latch_1_out_15[1]), .out_17(isWb), .in_9(Reset),
    .out_10(MA_RW_Instruction));
  Clock u_Clock (.out(Clock));
  Register #(.width(32)) PC (.D(multiplexer_1_out), .en(Stall), .Q(PC_q), .clk(Clock), .clr(Reset));
  Multiplexer #(.width(32), .enable("false")) multiplexer_1 (
    .in0(adder_1_out), .in1(branchTarget), .out(multiplexer_1_out), .sel(isBranchTaken));
  assign bit_extender_1_out = {{5{multiplexer_14_out[26]}}, {multiplexer_14_out[26], multiplexer_14_out_3, multiplexer_14_out_2, multiplexer_14_out[17:0]}};  // Bit_Extender bit_extender_1
  Multiplexer #(.select(2), .width(32), .enable("false")) multiplexer_2 (
    .in0(of_ex_latch_1_out_22), .in1(data), .in2(aluResult), .in3(aluResult), .out(multiplexer_2_out),
    .sel(RW_MA__EX_op2));
  Adder #(.width(32)) adder_1 (.a(32'h4), .b(PC_q), .out(adder_1_out));  // open: cin, cout
  Shifter #(.width(32)) shifter_1 (.in(bit_extender_1_out), .\dist (5'b00010), .out(shifter_1_out));
  Multiplexer #(.width(32), .enable("false")) multiplexer_3 (
    .in0(of_ex_latch_1_out_24), .in1(data), .out(multiplexer_3_out), .sel(RW__EX_op2));
  Multiplexer #(.select(2), .width(32), .enable("false")) multiplexer_4 (
    .in0(of_ex_latch_1_out_23), .in1(data), .in2(aluResult), .in3(aluResult), .out(multiplexer_4_out),
    .sel(RW_MA__EX_op1));
  ALU alu_1 (
    .A(multiplexer_4_out), .B(multiplexer_2_out), .ALUsignals(of_ex_latch_1_out_26),
    .aluResult(alu_1_aluresult), .is(alu_1_is), .is_2(alu_1_is_2));
  Adder #(.width(32)) adder_2 (.a(ma_rw_latch_1_out_11), .b(32'h4), .out(adder_2_out));  // open: cin, cout
  Calculate_Immediate calculate_immediate_1 (.imm(multiplexer_14_out[17:0]), .immx(calculate_immediate_1_immx));
  Adder #(.width(32)) adder_3 (.a(shifter_1_out), .b(if_of_latch_1_out_8), .out(adder_3_out));  // open: cin, cout
  Multiplexer #(.width(32), .enable("false")) multiplexer_5 (
    .in0(of_ex_latch_1_out_21), .in1(multiplexer_4_out), .out(branchTarget), .sel(of_ex_latch_1_out_27));
  Multiplexer #(.select(2), .width(32), .enable("false")) multiplexer_6 (
    .in0(ma_rw_latch_1_out_13), .in1(ma_rw_latch_1_out_12), .in2(adder_2_out), .out(data),
    .sel(ma_rw_latch_1_out_15));  // open: in3
  Multiplexer #(.width(32), .enable("false")) multiplexer_7 (
    .in0(multiplexer_9_out), .in1(calculate_immediate_1_immx), .out(multiplexer_7_out),
    .sel(control_unit_1_isimmediate));
  Flags flags_1 (
    .isCmp(of_ex_latch_1_out_26[0]), .is(alu_1_is), .is_2(alu_1_is_2), .flags_GT(flags_1_flags_gt),
    .flags_E(flags_1_flags_e));
  Memory_Unit memory_unit_1 (
    .MAR(aluResult), .ldResult(memory_unit_1_ldresult), .MDR(multiplexer_10_out),
    .isSt(ex_ma_latch_1_out_17), .isLd(ex_ma_latch_1_out_16), .Clock(Clock), .Reset(Reset));
  Multiplexer #(.width(4), .enable("false")) multiplexer_8 (
    .in0(multiplexer_14_out[17:14]), .in1(multiplexer_14_out_3), .out(multiplexer_8_out),
    .sel(control_unit_1_isst));
  Multiplexer #(.width(32), .enable("false")) multiplexer_9 (
    .in0(register_file_1_readd2), .in1(data), .out(multiplexer_9_out), .sel(RW__OF_op2));
  Multiplexer #(.width(32), .enable("false")) multiplexer_10 (
    .in0(ex_ma_latch_1_out_14), .in1(data), .out(multiplexer_10_out), .sel(RW__MA_op2));
  ROM #(.addrWidth(24), .dataWidth(32)) rom_1 (.addr(PC_q[25:2]), .data(rom_1_data));  // open: sel
  Multiplexer #(.width(4), .enable("false")) multiplexer_11 (
    .in0(multiplexer_14_out_2), .in1(4'b1111), .out(multiplexer_11_out), .sel(control_unit_1_isret));
  Register_File register_file_1 (
    .ReadA1(multiplexer_11_out), .ReadA2(multiplexer_8_out), .WriteE(isWb), .WriteD(data),
    .ReadD1(register_file_1_readd1), .ReadD2(register_file_1_readd2), .Clock(Clock), .Reset(Reset),
    .DisplayD(register_file_1_displayd), .DisplayA(Display_Address), .WriteA(\reg ));
  Multiplexer #(.width(32), .enable("false")) multiplexer_12 (
    .in0(register_file_1_readd1), .in1(data), .out(multiplexer_12_out), .sel(RW__OF_op1));
  Branch_Unit branch_unit_1 (
    .isBeq(of_ex_latch_1_out_28), .isUBranch(of_ex_latch_1_out_30), .flags_E(flags_1_flags_e),
    .isBgt(of_ex_latch_1_out_29), .flags_GT(flags_1_flags_gt), .isBranchTaken(isBranchTaken));
  Multiplexer #(.width(4), .enable("false")) multiplexer_13 (
    .in0(ma_rw_latch_1_out_14_2), .in1(4'b1111), .out(\reg ), .sel(ma_rw_latch_1_out_15[1]));
  Multiplexer #(.width(32), .enable("false")) multiplexer_14 (
    .in0(rom_1_data), .in1(32'h68000000),
    .out({multiplexer_14_out[31:26], multiplexer_14_out_3, multiplexer_14_out_2, multiplexer_14_out[17:0]}),
    .sel(isBranchTaken));
  Control_Unit control_unit_1 (
    .isSt(control_unit_1_isst), .isLd(control_unit_1_isld), .isBeq(control_unit_1_isbeq),
    .isBgt(control_unit_1_isbgt), .isRet(control_unit_1_isret), .I_bit(multiplexer_14_out[26]),
    .isImmediate(control_unit_1_isimmediate), .opcode(multiplexer_14_out[31:27]), .isWb(control_unit_1_iswb),
    .isUbranch(control_unit_1_isubranch), .isCall(control_unit_1_iscall),
    .ALUsignals(control_unit_1_alusignals));
  or or_1 (or_1_out, isBranchTaken, ~Stall);  // OR_Gate
  Hex_Digit_Display hex_digit_display_1 (.value(register_file_1_displayd[31:28]));  // open: dp
  Hex_Digit_Display hex_digit_display_2 (.value(data[31:28]));  // open: dp
  Hex_Digit_Display hex_digit_display_3 (.value(IF_OF_Instruction[31:28]));  // open: dp
  Hex_Digit_Display hex_digit_display_4 (.value(OF_EX_Instruction[31:28]));  // open: dp
  Hex_Digit_Display hex_digit_display_5 (.value(EX_MA_Instruction[31:28]));  // open: dp
  Hex_Digit_Display hex_digit_display_6 (.value(register_file_1_displayd[27:24]));  // open: dp
  Hex_Digit_Display hex_digit_display_7 (.value(data[27:24]));  // open: dp
  Hex_Digit_Display hex_digit_display_8 (.value(IF_OF_Instruction[27:24]));  // open: dp
  Hex_Digit_Display hex_digit_display_9 (.value(OF_EX_Instruction[27:24]));  // open: dp
  Hex_Digit_Display hex_digit_display_10 (.value(EX_MA_Instruction[27:24]));  // open: dp
  Hex_Digit_Display hex_digit_display_11 (.value(MA_RW_Instruction[27:24]));  // open: dp
  Hex_Digit_Display hex_digit_display_12 (.value(MA_RW_Instruction[31:28]));  // open: dp
  Hex_Digit_Display hex_digit_display_13 (.value(register_file_1_displayd[23:20]));  // open: dp
  Hex_Digit_Display hex_digit_display_14 (.value(data[23:20]));  // open: dp
  Hex_Digit_Display hex_digit_display_15 (.value(IF_OF_Instruction[23:20]));  // open: dp
  Hex_Digit_Display hex_digit_display_16 (.value(OF_EX_Instruction[23:20]));  // open: dp
  Hex_Digit_Display hex_digit_display_17 (.value(EX_MA_Instruction[23:20]));  // open: dp
  Hex_Digit_Display hex_digit_display_18 (.value(MA_RW_Instruction[23:20]));  // open: dp
  Hex_Digit_Display hex_digit_display_19 (.value(register_file_1_displayd[15:12]));  // open: dp
  Hex_Digit_Display hex_digit_display_20 (.value(register_file_1_displayd[19:16]));  // open: dp
  Hex_Digit_Display hex_digit_display_21 (.value(data[19:16]));  // open: dp
  Hex_Digit_Display hex_digit_display_22 (.value(data[15:12]));  // open: dp
  Hex_Digit_Display hex_digit_display_23 (.value(IF_OF_Instruction[19:16]));  // open: dp
  Hex_Digit_Display hex_digit_display_24 (.value(IF_OF_Instruction[15:12]));  // open: dp
  Hex_Digit_Display hex_digit_display_25 (.value(OF_EX_Instruction[19:16]));  // open: dp
  Hex_Digit_Display hex_digit_display_26 (.value(OF_EX_Instruction[15:12]));  // open: dp
  Hex_Digit_Display hex_digit_display_27 (.value(EX_MA_Instruction[19:16]));  // open: dp
  Hex_Digit_Display hex_digit_display_28 (.value(EX_MA_Instruction[15:12]));  // open: dp
  Hex_Digit_Display hex_digit_display_29 (.value(MA_RW_Instruction[19:16]));  // open: dp
  Hex_Digit_Display hex_digit_display_30 (.value(register_file_1_displayd[11:8]));  // open: dp
  Hex_Digit_Display hex_digit_display_31 (.value(data[11:8]));  // open: dp
  Hex_Digit_Display hex_digit_display_32 (.value(IF_OF_Instruction[11:8]));  // open: dp
  Hex_Digit_Display hex_digit_display_33 (.value(OF_EX_Instruction[11:8]));  // open: dp
  Hex_Digit_Display hex_digit_display_34 (.value(EX_MA_Instruction[11:8]));  // open: dp
  Hex_Digit_Display hex_digit_display_35 (.value(MA_RW_Instruction[11:8]));  // open: dp
  Hex_Digit_Display hex_digit_display_36 (.value(MA_RW_Instruction[15:12]));  // open: dp
  Hex_Digit_Display hex_digit_display_37 (.value(register_file_1_displayd[7:4]));  // open: dp
  Hex_Digit_Display hex_digit_display_38 (.value(data[7:4]));  // open: dp
  Hex_Digit_Display hex_digit_display_39 (.value(IF_OF_Instruction[7:4]));  // open: dp
  Hex_Digit_Display hex_digit_display_40 (.value(OF_EX_Instruction[7:4]));  // open: dp
  Hex_Digit_Display hex_digit_display_41 (.value(EX_MA_Instruction[7:4]));  // open: dp
  Hex_Digit_Display hex_digit_display_42 (.value(MA_RW_Instruction[7:4]));  // open: dp
  Hex_Digit_Display hex_digit_display_43 (.value(register_file_1_displayd[3:0]));  // open: dp
  Hex_Digit_Display hex_digit_display_44 (.value(data[3:0]));  // open: dp
  Hex_Digit_Display hex_digit_display_45 (.value(IF_OF_Instruction[3:0]));  // open: dp
  Hex_Digit_Display hex_digit_display_46 (.value(OF_EX_Instruction[3:0]));  // open: dp
  Hex_Digit_Display hex_digit_display_47 (.value(EX_MA_Instruction[3:0]));  // open: dp
  Hex_Digit_Display hex_digit_display_48 (.value(MA_RW_Instruction[3:0]));  // open: dp
  Forwarding_Unit forwarding_unit_1 (
    .MA_RW(MA_RW_Instruction), .EX_MA(EX_MA_Instruction), .OF_EX(OF_EX_Instruction),
    .IF_OF(IF_OF_Instruction), .RW__OF_op1(RW__OF_op1), .RW__OF_op2(RW__OF_op2),
    .RW_MA__EX_op1(RW_MA__EX_op1), .RW__EX_op2(RW__EX_op2), .RW_MA__EX_op2(RW_MA__EX_op2),
    .RW__MA_op2(RW__MA_op2));
  not not_1 (Stall, data_lock_unit_1_data_lock_conflict);
  Data_Lock_Unit data_lock_unit_1 (
    .IF_OF(IF_OF_Instruction), .OF_EX(OF_EX_Instruction),
    .Data_Lock_Conflict(data_lock_unit_1_data_lock_conflict));

  // Notes on the sheet:
  //   ALUsignals
  //   B
  //   pc
  //   pc+4
  //   branchTarget
  //   offset
  //   pc
  //   branchTarget
  //   A
  //   ALU
  //   aluResult
  //   MAR
  //   calc immx
  //   imm
  //   isRet
  //   is>
  //   is=
  //   MDR
  //   Memory
  //   Unit
  //   ldResult
  //   data
  //   معماری پردازنده                  با پایپلاین 5 مرحله ای
  //   immx
  //   Flags
  //   isCmp
  //   isLd
  //   isSt
  //   isLd
  //   isCall
  //   RISC V
  //   Instruction Memory
  //   rs2
  //   rd
  //   isSt
  //   Register
  //   File
  //   op2
  //   isImmediate
  //   flags(GT)
  //   flags(E)
  //   contents of rom_1 (hex, n*v repeats v):
  //   100093 200113 300193 3100b3
  //   instruction
  //   isRet
  //   E
  //   A
  //   data
  //   address
  //   D
  //   op1
  //   Branch
  //   Unit
  //   opcode
  //   I bit
  //   isWb
  //   isBeq
  //   isBgt
  //   isUBranch
  //   CONTROL
  //   UNIT
  //   Display Register
  //   Display Register
  //   Display Register
  //   Display Register
  //   Display Register
  //   Display Register
endmodule

module Control_Unit (
  input  I_bit,
  input  [4:0] opcode,
  output isSt,
  output isLd,
  output isBeq,
  output isBgt,
  output isRet,
  output isImmediate,
  output isWb,
  output isUbranch,
  output isCall,
  output [12:0] ALUsignals
);

  wire and_6_out, and_7_out, and_8_out, and_9_out, and_10_out, and_12_out, and_13_out, nand_1_out;

  nand nand_1 (nand_1_out, opcode[0], opcode[1]);
  and and_1 (isSt, opcode[0], opcode[1], opcode[2], opcode[3], ~opcode[4]);  // AND_Gate
  and and_2 (isLd, ~opcode[0], opcode[1], opcode[2], opcode[3], ~opcode[4]);  // AND_Gate
  and and_3 (isBeq, ~opcode[0], ~opcode[1], ~opcode[2], ~opcode[3], opcode[4]);  // AND_Gate
  and and_4 (isBgt, opcode[0], ~opcode[1], ~opcode[2], ~opcode[3], opcode[4]);  // AND_Gate
  and and_5 (isRet, ~opcode[0], ~opcode[1], opcode[2], ~opcode[3], opcode[4]);  // AND_Gate
  and and_6 (and_6_out, opcode[0], ~opcode[1], opcode[2], ~opcode[4]);  // AND_Gate
  and and_7 (and_7_out, opcode[0], opcode[2], opcode[3], ~opcode[4]);  // AND_Gate
  and and_8 (and_8_out, opcode[4], nand_1_out);
  and and_9 (and_9_out, opcode[1], ~opcode[2], ~opcode[3], opcode[4]);  // AND_Gate
  and and_10 (and_10_out, ~opcode[0], ~opcode[1], opcode[2], ~opcode[3], opcode[4]);  // AND_Gate
  and and_11 (isCall, opcode[0], opcode[1], ~opcode[2], ~opcode[3], opcode[4]);  // AND_Gate
  and and_12 (and_12_out, ~opcode[0], ~opcode[1], ~opcode[2], ~opcode[3], ~opcode[4]);  // AND_Gate
  and and_13 (and_13_out, opcode[1], opcode[2], opcode[3], ~opcode[4]);  // AND_Gate
  and isSub (ALUsignals[2], opcode[0], ~opcode[1], ~opcode[2], ~opcode[3], ~opcode[4]);  // AND_Gate
  and isCmp (ALUsignals[0], opcode[0], ~opcode[1], opcode[2], ~opcode[3], ~opcode[4]);  // AND_Gate
  and isMul (ALUsignals[3], ~opcode[0], opcode[1], ~opcode[2], ~opcode[3], ~opcode[4]);  // AND_Gate
  and isDiv (ALUsignals[4], opcode[0], opcode[1], ~opcode[2], ~opcode[3], ~opcode[4]);  // AND_Gate
  and isMod (ALUsignals[5], ~opcode[0], ~opcode[1], opcode[2], ~opcode[3], ~opcode[4]);  // AND_Gate
  and isLsl (ALUsignals[7], ~opcode[0], opcode[1], ~opcode[2], opcode[3], ~opcode[4]);  // AND_Gate
  and isLsr (ALUsignals[8], opcode[0], opcode[1], ~opcode[2], opcode[3], ~opcode[4]);  // AND_Gate
  and isAsr (ALUsignals[9], ~opcode[0], ~opcode[1], opcode[2], opcode[3], ~opcode[4]);  // AND_Gate
  and isOr (ALUsignals[12], opcode[0], opcode[1], opcode[2], ~opcode[3], ~opcode[4]);  // AND_Gate
  and isAnd (ALUsignals[11], ~opcode[0], opcode[1], opcode[2], ~opcode[3], ~opcode[4]);  // AND_Gate
  and isNot (ALUsignals[10], ~opcode[0], ~opcode[1], ~opcode[2], opcode[3], ~opcode[4]);  // AND_Gate
  and isMov (ALUsignals[6], opcode[0], ~opcode[1], ~opcode[2], opcode[3], ~opcode[4]);  // AND_Gate
  or or_1 (isUbranch, and_9_out, and_10_out);
  or isAdd (ALUsignals[1], and_12_out, and_13_out);
  nor nor_1 (isWb, and_6_out, and_7_out, and_8_out);

  assign isImmediate = I_bit;

  // Notes on the sheet:
  //   op1
  //   op2
  //   op3
  //   op4
  //   op5
endmodule

module Register_File (
  input  Clock,
  input  Reset,
  input  [31:0] WriteD,
  input  [3:0] ReadA1,
  input  WriteE,
  input  [3:0] WriteA,
  input  [3:0] ReadA2,
  input  [3:0] DisplayA,
  output [31:0] ReadD1,
  output [31:0] ReadD2,
  output [31:0] DisplayD
);

  wire demultiplexer_1_out0, demultiplexer_1_out1, demultiplexer_1_out2, demultiplexer_1_out3,
       demultiplexer_1_out4, demultiplexer_1_out5, demultiplexer_1_out6, demultiplexer_1_out7,
       demultiplexer_1_out8, demultiplexer_1_out9, demultiplexer_1_out10, demultiplexer_1_out11,
       demultiplexer_1_out12, demultiplexer_1_out13, demultiplexer_1_out14, demultiplexer_1_out15,
       multiplexer_2_out, or_1_out, or_2_out;
  wire [31:0] multiplexer_1_out, r0_q, r1_q, r2_q, r3_q, r4_q, r5_q, r6_q, r7_q, r8_q, r9_q, r10_q, r11_q,
       r12_q, r13_q, r14_q, r15_q;

  Demultiplexer #(.select(4), .disabled(0), .enable("false")) demultiplexer_1 (
    .out0(demultiplexer_1_out0), .out1(demultiplexer_1_out1), .out2(demultiplexer_1_out2),
    .out3(demultiplexer_1_out3), .out4(demultiplexer_1_out4), .out5(demultiplexer_1_out5),
    .out6(demultiplexer_1_out6), .out7(demultiplexer_1_out7), .out8(demultiplexer_1_out8),
    .out9(demultiplexer_1_out9), .out10(demultiplexer_1_out10), .out11(demultiplexer_1_out11),
    .out12(demultiplexer_1_out12), .out13(demultiplexer_1_out13), .out14(demultiplexer_1_out14),
    .out15(demultiplexer_1_out15), .in(WriteE), .sel(WriteA));
  Multiplexer #(.width(32), .enable("false")) multiplexer_1 (
    .in0(WriteD), .in1(32'h3fffffc), .out(multiplexer_1_out), .sel(Reset));
  or or_1 (or_1_out, demultiplexer_1_out14, Reset);
  or or_2 (or_2_out, Clock, Reset);
  Multiplexer #(.enable("false")) multiplexer_2 (.in0(or_2_out), .out(multiplexer_2_out), .sel(1'b0));  // open: in1
  Register #(.width(32)) r0 (.D(WriteD), .en(demultiplexer_1_out0), .Q(r0_q), .clk(Clock), .clr(Reset));
  Register #(.width(32)) r1 (.D(WriteD), .en(demultiplexer_1_out1), .Q(r1_q), .clk(Clock), .clr(Reset));
  Register #(.width(32)) r2 (.D(WriteD), .en(demultiplexer_1_out2), .Q(r2_q), .clk(Clock), .clr(Reset));
  Register #(.width(32)) r3 (.D(WriteD), .en(demultiplexer_1_out3), .Q(r3_q), .clk(Clock), .clr(Reset));
  Register #(.width(32)) r4 (.D(WriteD), .en(demultiplexer_1_out4), .Q(r4_q), .clk(Clock), .clr(Reset));
  Register #(.width(32)) r5 (.D(WriteD), .en(demultiplexer_1_out5), .Q(r5_q), .clk(Clock), .clr(Reset));
  Register #(.width(32)) r6 (.D(WriteD), .en(demultiplexer_1_out6), .Q(r6_q), .clk(Clock), .clr(Reset));
  Register #(.width(32)) r7 (.D(WriteD), .en(demultiplexer_1_out7), .Q(r7_q), .clk(Clock), .clr(Reset));
  Register #(.width(32)) r8 (.D(WriteD), .en(demultiplexer_1_out8), .Q(r8_q), .clk(Clock), .clr(Reset));
  Register #(.width(32)) r9 (.D(WriteD), .en(demultiplexer_1_out9), .Q(r9_q), .clk(Clock), .clr(Reset));
  Register #(.width(32)) r10 (.D(WriteD), .en(demultiplexer_1_out10), .Q(r10_q), .clk(Clock), .clr(Reset));
  Register #(.width(32)) r11 (.D(WriteD), .en(demultiplexer_1_out11), .Q(r11_q), .clk(Clock), .clr(Reset));
  Register #(.width(32)) r12 (.D(WriteD), .en(demultiplexer_1_out12), .Q(r12_q), .clk(Clock), .clr(Reset));
  Register #(.width(32)) r13 (.D(WriteD), .en(demultiplexer_1_out13), .Q(r13_q), .clk(Clock), .clr(Reset));
  Register #(.width(32)) r14 (.D(multiplexer_1_out), .en(or_1_out), .Q(r14_q), .clk(multiplexer_2_out));  // open: clr
  Register #(.width(32)) r15 (.D(WriteD), .en(demultiplexer_1_out15), .Q(r15_q), .clk(Clock), .clr(Reset));
  Multiplexer #(.select(4), .width(32), .disabled(0), .enable("false")) multiplexer_3 (
    .in0(r0_q), .in1(r1_q), .in2(r2_q), .in3(r3_q), .in4(r4_q), .in5(r5_q), .in6(r6_q), .in7(r7_q),
    .in8(r8_q), .in9(r9_q), .in10(r10_q), .in11(r11_q), .in12(r12_q), .in13(r13_q), .in14(r14_q),
    .in15(r15_q), .out(ReadD1), .sel(ReadA1));
  Multiplexer #(.select(4), .width(32), .disabled(0), .enable("false")) multiplexer_4 (
    .in0(r0_q), .in1(r1_q), .in2(r2_q), .in3(r3_q), .in4(r4_q), .in5(r5_q), .in6(r6_q), .in7(r7_q),
    .in8(r8_q), .in9(r9_q), .in10(r10_q), .in11(r11_q), .in12(r12_q), .in13(r13_q), .in14(r14_q),
    .in15(r15_q), .out(ReadD2), .sel(ReadA2));
  Multiplexer #(.select(4), .width(32), .disabled(0), .enable("false")) multiplexer_5 (
    .in0(r0_q), .in1(r1_q), .in2(r2_q), .in3(r3_q), .in4(r4_q), .in5(r5_q), .in6(r6_q), .in7(r7_q),
    .in8(r8_q), .in9(r9_q), .in10(r10_q), .in11(r11_q), .in12(r12_q), .in13(r13_q), .in14(r14_q),
    .in15(r15_q), .out(DisplayD), .sel(DisplayA));
endmodule

module ALU (
  input  [31:0] A,
  input  [31:0] B,
  input  [12:0] ALUsignals,
  output [31:0] aluResult,
  output is,
  output is_2
);

  wire [31:0] adder_1_out, and_1_out, divider_1_out, divider_1_rem, multiplier_1_out, not_1_out, or_1_out,
       shifter_1_out, shifter_2_out, shifter_3_out, subtractor_1_out;

  Adder #(.width(32)) adder_1 (.a(A), .b(B), .out(adder_1_out));  // open: cin, cout
  Subtractor #(.width(32)) subtractor_1 (.a(A), .b(B), .out(subtractor_1_out));  // open: bin, bout
  Multiplier #(.width(32)) multiplier_1 (.a(A), .b(B), .out(multiplier_1_out));  // open: cin, cout
  Divider #(.width(32)) divider_1 (.a(A), .b(B), .out(divider_1_out), .rem(divider_1_rem));  // open: upper
  Comparator #(.width(32)) comparator_1 (.a(A), .b(B), .gt(is), .eq(is_2));  // open: lt
  Shifter #(.width(32)) shifter_1 (.in(A), .\dist (B[4:0]), .out(shifter_1_out));
  Shifter #(.width(32), .shift("lr")) shifter_2 (.in(A), .\dist (B[4:0]), .out(shifter_2_out));
  Shifter #(.width(32), .shift("ar")) shifter_3 (.in(A), .\dist (B[4:0]), .out(shifter_3_out));
  assign not_1_out = ~B;  // NOT_Gate not_1, 32 bits wide
  assign and_1_out = A & B;  // AND_Gate and_1, 32 bits wide
  assign or_1_out = A | B;  // OR_Gate or_1, 32 bits wide
  assign aluResult = ALUsignals[1] ? adder_1_out : 32'bz;  // Controlled_Buffer controlled_buffer_1
  assign aluResult = ALUsignals[2] ? subtractor_1_out : 32'bz;  // Controlled_Buffer controlled_buffer_2
  assign aluResult = ALUsignals[3] ? multiplier_1_out : 32'bz;  // Controlled_Buffer controlled_buffer_3
  assign aluResult = ALUsignals[4] ? divider_1_out : 32'bz;  // Controlled_Buffer controlled_buffer_4
  assign aluResult = ALUsignals[5] ? divider_1_rem : 32'bz;  // Controlled_Buffer controlled_buffer_5
  assign aluResult = ALUsignals[6] ? B : 32'bz;  // Controlled_Buffer controlled_buffer_6
  assign aluResult = ALUsignals[7] ? shifter_1_out : 32'bz;  // Controlled_Buffer controlled_buffer_7
  assign aluResult = ALUsignals[8] ? shifter_2_out : 32'bz;  // Controlled_Buffer controlled_buffer_8
  assign aluResult = ALUsignals[9] ? shifter_3_out : 32'bz;  // Controlled_Buffer controlled_buffer_9
  assign aluResult = ALUsignals[10] ? not_1_out : 32'bz;  // Controlled_Buffer controlled_buffer_10
  assign aluResult = ALUsignals[11] ? and_1_out : 32'bz;  // Controlled_Buffer controlled_buffer_11
  assign aluResult = ALUsignals[12] ? or_1_out : 32'bz;  // Controlled_Buffer controlled_buffer_12

  // Notes on the sheet:
  //   add
  //   sub
  //   mul
  //   div
  //   cmp
  //   lsr
  //   mod
  //   lsl
  //   asr
endmodule

module Flags (
  input  isCmp,
  input  is,
  input  is_2,
  output flags_GT,
  output flags_E
);

  D_Flip_Flop #(.trigger("high")) d_ff_1 (.clk(isCmp), .D(is), .Q(flags_GT));  // open: Qn, preset, en, reset
  D_Flip_Flop #(.trigger("high")) d_ff_2 (.clk(isCmp), .D(is_2), .Q(flags_E));  // open: Qn, preset, en, reset
endmodule

module Branch_Unit (
  input  isUBranch,
  input  isBeq,
  input  flags_E,
  input  isBgt,
  input  flags_GT,
  output isBranchTaken
);

  wire and_1_out, and_2_out;

  and and_1 (and_1_out, isBeq, flags_E);
  and and_2 (and_2_out, isBgt, flags_GT);
  or or_1 (isBranchTaken, isUBranch, and_1_out, and_2_out);
endmodule

module Memory_Unit (
  input  [31:0] MAR,
  input  isLd,
  input  [31:0] MDR,
  input  isSt,
  input  Clock,
  input  Reset,
  output [31:0] ldResult
);

  RAM #(.addrWidth(24), .dataWidth(32), .bus("separate")) ram_1 (
    .addr(MAR[25:2]), .din(MDR), .data(ldResult), .str(isSt), .clk(Clock), .ld(isLd), .clr(Reset));  // open: sel
endmodule

module IF_OF_Latch (
  input  Stall,
  input  [31:0] in_2,
  input  [31:0] in_3,
  input  in_4,
  input  in_5,
  output [31:0] out_6,
  output [31:0] out_7,
  output [31:0] out_8
);

  Register #(.width(32)) register_1 (.D(in_2), .en(Stall), .Q(out_8), .clk(in_4), .clr(in_5));
  Register #(.width(32)) register_2 (.D(in_3), .en(Stall), .Q(out_6), .clk(in_4), .clr(in_5));

  assign out_7 = out_6;
endmodule

module Calculate_Immediate (
  input  [17:0] imm,
  output [31:0] immx
);

  wire [31:0] bit_extender_1_out, bit_extender_2_out, shifter_1_out;

  assign bit_extender_1_out = {{16{1'b0}}, imm[15:0]};  // Bit_Extender bit_extender_1
  assign bit_extender_2_out = {{16{imm[15]}}, imm[15:0]};  // Bit_Extender bit_extender_2
  Shifter #(.width(32)) shifter_1 (.in(bit_extender_1_out), .\dist (5'b10000), .out(shifter_1_out));
  Multiplexer #(.select(2), .width(32), .enable("false")) multiplexer_1 (
    .in0(bit_extender_2_out), .in1(bit_extender_1_out), .in2(shifter_1_out), .out(immx), .sel(imm[17:16]));  // open: in3

  // Notes on the sheet:
  //   modifier bits
  //   high
  //   default
  //   unsigned
endmodule

module OF_EX_Latch (
  input  in_1,
  input  [12:0] in_2,
  input  Bubble,
  input  [31:0] in_4,
  input  [31:0] in_5,
  input  [31:0] in_6,
  input  [31:0] in_7,
  input  [31:0] in_8,
  input  [31:0] isRet,
  input  in_10,
  input  isBgt,
  input  isUBranch,
  input  isLd,
  input  isSt,
  input  in_15,
  input  in_16,
  input  in_17,
  input  in_18,
  output [31:0] out_19,
  output [31:0] out_20,
  output [31:0] out_21,
  output [31:0] out_22,
  output [31:0] out_23,
  output [31:0] out_24,
  output [31:0] out_25,
  output [12:0] out_26,
  output out_27,
  output out_28,
  output out_29,
  output out_30,
  output out_31,
  output out_32,
  output out_33,
  output out_34
);

  wire [31:0] multiplexer_1_out;

  Register #(.width(32)) register_1 (.D(in_4), .Q(out_20), .clk(in_17), .clr(in_18));  // open: en
  Register #(.width(32)) register_2 (.D(in_5), .Q(out_21), .clk(in_17), .clr(in_18));  // open: en
  Register #(.width(32)) register_3 (.D(in_6), .Q(out_22), .clk(in_17), .clr(in_18));  // open: en
  Register #(.width(32)) register_4 (.D(in_7), .Q(out_23), .clk(in_17), .clr(in_18));  // open: en
  Register #(.width(32)) register_5 (.D(in_8), .Q(out_24), .clk(in_17), .clr(in_18));  // open: en
  Multiplexer #(.width(32), .enable("false")) multiplexer_1 (
    .in0(isRet), .in1(32'h68000000), .out(multiplexer_1_out), .sel(Bubble));
  Register #(.width(32)) register_6 (.D(multiplexer_1_out), .Q(out_19), .clk(in_17), .clr(in_18));  // open: en
  Control_Packet control_packet_1 (
    .Bubble(Bubble), .in_11(in_17), .in_12(in_18), .isRet(in_1), .in_9(in_2), .in_1(in_10), .isBgt(isBgt),
    .isUBranch(isUBranch), .isLd(isLd), .isSt(isSt), .in_6(in_15), .in_7(in_16), .out_14(out_27),
    .out_13(out_26), .out_15(out_28), .out_16(out_29), .out_17(out_30), .out_18(out_31), .out_19(out_32),
    .out_20(out_33), .out_21(out_34));

  assign out_25 = out_19;

  // Notes on the sheet:
  //   PC
  //   Branch Target
  //   B
  //   A
  //   OP2
  //   INSTRUCTION
  //   ALU Signals
  //   isBeq
  //   isCall
  //   isWb
endmodule

module EX_MA_Latch (
  input  isCall,
  input  isLd,
  input  isSt,
  input  isWb,
  input  [31:0] in_5,
  input  [31:0] in_6,
  input  [31:0] in_7,
  input  [31:0] in_8,
  input  in_9,
  input  in_10,
  output [31:0] out_11,
  output [31:0] out_12,
  output [31:0] out_13,
  output [31:0] out_14,
  output [31:0] out_15,
  output out_16,
  output out_17,
  output out_18,
  output out_19
);

  Register #(.width(32)) register_1 (.D(in_5), .Q(out_12), .clk(in_9), .clr(in_10));  // open: en
  Register #(.width(32)) register_2 (.D(in_6), .Q(out_13), .clk(in_9), .clr(in_10));  // open: en
  Register #(.width(32)) register_3 (.D(in_7), .Q(out_14), .clk(in_9), .clr(in_10));  // open: en
  Register #(.width(32)) register_4 (.D(in_8), .Q(out_11), .clk(in_9), .clr(in_10));  // open: en
  Register #(.width(1)) register_5 (.D(isLd), .Q(out_16), .clk(in_9), .clr(in_10));  // open: en
  Register #(.width(1)) register_6 (.D(isSt), .Q(out_17), .clk(in_9), .clr(in_10));  // open: en
  Register #(.width(1)) register_7 (.D(isCall), .Q(out_18), .clk(in_9), .clr(in_10));  // open: en
  Register #(.width(1)) register_8 (.D(isWb), .Q(out_19), .clk(in_9), .clr(in_10));  // open: en

  assign out_15 = out_11;

  // Notes on the sheet:
  //   PC
  //   Alu Result
  //   OP2
  //   INSTRUCTION
endmodule

module MA_RW_Latch (
  input  isCall,
  input  isLd,
  input  isWb,
  input  [31:0] in_4,
  input  [31:0] in_5,
  input  [31:0] in_6,
  input  [31:0] in_7,
  input  in_8,
  input  in_9,
  output [31:0] out_10,
  output [31:0] out_11,
  output [31:0] out_12,
  output [31:0] out_13,
  output [31:0] out_14,
  output out_15,
  output out_16,
  output out_17
);

  Register #(.width(32)) register_1 (.D(in_4), .Q(out_11), .clk(in_8), .clr(in_9));  // open: en
  Register #(.width(32)) register_2 (.D(in_5), .Q(out_12), .clk(in_8), .clr(in_9));  // open: en
  Register #(.width(32)) register_3 (.D(in_6), .Q(out_13), .clk(in_8), .clr(in_9));  // open: en
  Register #(.width(32)) register_4 (.D(in_7), .Q(out_10), .clk(in_8), .clr(in_9));  // open: en
  Register #(.width(1)) register_5 (.D(isLd), .Q(out_15), .clk(in_8), .clr(in_9));  // open: en
  Register #(.width(1)) register_6 (.D(isCall), .Q(out_16), .clk(in_8), .clr(in_9));  // open: en
  Register #(.width(1)) register_7 (.D(isWb), .Q(out_17), .clk(in_8), .clr(in_9));  // open: en

  assign out_14 = out_10;

  // Notes on the sheet:
  //   PC
  //   LoadResult
  //   Alu Result
  //   INSTRUCTION
endmodule

module Conflict_Detection_Unit (
  input  [31:0] A,
  input  [31:0] B,
  output FO_Conflict,
  output SO_Conflict
);

  wire and_1_out, and_2_out, and_3_out, check_opcode_a_op1_1_out_2, check_opcode_a_op2_1_out_2,
       check_opcode_b_1_out_2, compare_4_bit_1_out_3, compare_4_bit_2_out_3, instruction_split_a_1_hassrc2;
  wire [3:0] instruction_split_a_1_src2, instruction_split_a_1_src_1, instruction_split_b_1_dest;

  Check_OPcode_A_op1 check_opcode_a_op1_1 (.in_1(A[31:27]), .out_2(check_opcode_a_op1_1_out_2));
  and and_1 (and_1_out, check_opcode_a_op1_1_out_2, check_opcode_b_1_out_2);
  Check_OPcode__A_op2 check_opcode_a_op2_1 (.in_1(A[31:27]), .out_2(check_opcode_a_op2_1_out_2));
  and and_2 (and_2_out, check_opcode_a_op2_1_out_2, check_opcode_b_1_out_2);
  Instruction_split_A instruction_split_a_1 (
    .A_opcode(A[31:27]), .A_A_opcode(A[26:0]), .Src_1(instruction_split_a_1_src_1),
    .hasSrc2(instruction_split_a_1_hassrc2), .Src2(instruction_split_a_1_src2));
  Check_OPcode__B check_opcode_b_1 (.in_1(B[31:27]), .out_2(check_opcode_b_1_out_2));
  Compare_4_bit compare_4_bit_1 (
    .in_1(instruction_split_a_1_src_1), .in_2(instruction_split_b_1_dest), .out_3(compare_4_bit_1_out_3));
  Multiplexer #(.enable("false")) multiplexer_1 (
    .in0(1'b0), .in1(compare_4_bit_1_out_3), .out(FO_Conflict), .sel(and_1_out));
  Instruction_split_B instruction_split_b_1 (
    .B_opcode(B[31:27]), .B___opcode(B[26:0]), .dest(instruction_split_b_1_dest));
  Compare_4_bit compare_4_bit_2 (
    .in_1(instruction_split_a_1_src2), .in_2(instruction_split_b_1_dest), .out_3(compare_4_bit_2_out_3));
  and and_3 (and_3_out, instruction_split_a_1_hassrc2, compare_4_bit_2_out_3);
  Multiplexer #(.enable("false")) multiplexer_2 (.in0(1'b0), .in1(and_3_out), .out(SO_Conflict), .sel(and_2_out));

  // Notes on the sheet:
  //   src1
  //   src2
  //   hassrc2
  //   dest
endmodule

module Check_OPcode__A_op2 (
  input  [4:0] in_1,
  output out_2
);

  wire isBeq_isB__isBgt__is_isCall_out, isNop_out;

  and isBeq_isB__isBgt__is_isCall (isBeq_isB__isBgt__is_isCall_out, in_1[4], ~in_1[3], ~in_1[2]);  // AND_Gate
  nor nor_1 (out_2, isBeq_isB__isBgt__is_isCall_out, isNop_out);
  and isNop (isNop_out, ~in_1[4], in_1[3], in_1[2], ~in_1[1], in_1[0]);  // AND_Gate
endmodule

module Check_OPcode__B (
  input  [4:0] in_1,
  output out_2
);

  wire and_1_out, and_2_out, and_3_out, and_4_out, and_5_out;

  and and_1 (and_1_out, ~in_1[4], in_1[2], ~in_1[1], in_1[0]);  // AND_Gate
  and and_2 (and_2_out, ~in_1[4], in_1[3], in_1[2], in_1[0]);  // AND_Gate
  nor nor_1 (out_2, and_1_out, and_2_out, and_3_out, and_4_out, and_5_out);
  and and_3 (and_3_out, in_1[4], ~in_1[3], ~in_1[2], ~in_1[1]);  // AND_Gate
  and and_4 (and_4_out, in_1[4], ~in_1[3], ~in_1[2], ~in_1[0]);  // AND_Gate
  and and_5 (and_5_out, in_1[4], ~in_1[3], ~in_1[1], ~in_1[0]);  // AND_Gate

  // Notes on the sheet:
  //   nop,cmp,st,b,beq,bgt,ret
endmodule

module Instruction_split_A (
  input  [4:0] A_opcode,
  input  [26:0] A_A_opcode,
  output [3:0] Src_1,
  output [3:0] Src2,
  output hasSrc2
);

  wire isRet_out, isSt_out, not_1_out;

  and isRet (isRet_out, A_opcode[4], ~A_opcode[3], A_opcode[2], ~A_opcode[1], ~A_opcode[0]);  // AND_Gate
  and isSt (isSt_out, ~A_opcode[4], A_opcode[3], A_opcode[2], A_opcode[1], A_opcode[0]);  // AND_Gate
  Multiplexer #(.width(4), .enable("false")) multiplexer_1 (
    .in0(A_A_opcode[21:18]), .in1(4'b1111), .out(Src_1), .sel(isRet_out));
  not not_1 (not_1_out, A_A_opcode[26]);
  Multiplexer #(.enable("false")) multiplexer_2 (.in0(not_1_out), .in1(1'b1), .out(hasSrc2), .sel(isSt_out));
  Multiplexer #(.width(4), .enable("false")) multiplexer_3 (
    .in0(A_A_opcode[17:14]), .in1(A_A_opcode[25:22]), .out(Src2), .sel(isSt_out));

  // Notes on the sheet:
  //   A.rs1
  //   ra
  //   A.I
  //   A.rs2
  //   A.rd
endmodule

module Instruction_split_B (
  input  [4:0] B_opcode,
  input  [26:0] B___opcode,
  output [3:0] dest
);

  wire isCall_out;

  and isCall (isCall_out, B_opcode[4], ~B_opcode[3], ~B_opcode[2], B_opcode[1], B_opcode[0]);  // AND_Gate
  Multiplexer #(.width(4), .enable("false")) multiplexer_1 (
    .in0(B___opcode[25:22]), .in1(4'b1111), .out(dest), .sel(isCall_out));

  // Notes on the sheet:
  //   ra
  //   rd
endmodule

module Compare_4_bit (
  input  [3:0] in_1,
  input  [3:0] in_2,
  output out_3
);

  wire [3:0] subtractor_1_out;

  Subtractor #(.width(4)) subtractor_1 (.a(in_2), .b(in_1), .out(subtractor_1_out));  // open: bin, bout
  nor nor_1 (out_3, subtractor_1_out[3], subtractor_1_out[2], subtractor_1_out[1], subtractor_1_out[0]);
endmodule

module Data_Lock_Unit (
  input  [31:0] IF_OF,
  input  [31:0] OF_EX,
  output Data_Lock_Conflict
);

  wire and_1_out, and_2_out, check_opcode_a_op1_1_out_2, check_opcode_a_op2_1_out_2, isLd_out, isSt_out,
       not_1_out, or_1_out, src1_vs_dest_out_3, src2_vs_dest_out_3;

  Check_OPcode_A_op1 check_opcode_a_op1_1 (.in_1(IF_OF[4:0]), .out_2(check_opcode_a_op1_1_out_2));
  and isLd (isLd_out, ~OF_EX[27], OF_EX[28], OF_EX[29], OF_EX[30], ~OF_EX[31]);  // AND_Gate
  not not_1 (not_1_out, isSt_out);
  and isSt (isSt_out, IF_OF[0], IF_OF[1], IF_OF[2], IF_OF[3], ~IF_OF[4]);  // AND_Gate
  Compare_4_bit src1_vs_dest (.in_1(OF_EX[25:22]), .in_2(IF_OF[21:18]), .out_3(src1_vs_dest_out_3));
  and and_1 (and_1_out, src1_vs_dest_out_3, check_opcode_a_op1_1_out_2);
  Compare_4_bit src2_vs_dest (.in_1(OF_EX[25:22]), .in_2(IF_OF[17:14]), .out_3(src2_vs_dest_out_3));
  and and_2 (and_2_out, src2_vs_dest_out_3, check_opcode_a_op2_1_out_2);
  or or_1 (or_1_out, and_2_out, and_1_out);
  and and_3 (Data_Lock_Conflict, or_1_out, isLd_out);
  Check_OPcode__A_op2 check_opcode_a_op2_1 (.in_1(IF_OF[4:0]), .out_2(check_opcode_a_op2_1_out_2));
endmodule

module Forwarding_Unit (
  input  [31:0] MA_RW,
  input  [31:0] EX_MA,
  input  [31:0] OF_EX,
  input  [31:0] IF_OF,
  output RW__OF_op2,
  output RW__OF_op1,
  output [1:0] RW_MA__EX_op1,
  output RW__EX_op2,
  output RW__MA_op2,
  output [1:0] RW_MA__EX_op2
);

  wire and_1_out, conflict_detection_unit_2_so_conflict;

  Conflict_Detection_Unit conflict_detection_unit_1 (
    .A(EX_MA), .B(MA_RW), .SO_Conflict(RW__MA_op2));  // open: FO_Conflict
  Conflict_Detection_Unit conflict_detection_unit_2 (
    .A(OF_EX), .B(EX_MA), .FO_Conflict(RW_MA__EX_op1[1]), .SO_Conflict(conflict_detection_unit_2_so_conflict));
  and and_1 (and_1_out, ~OF_EX[31], OF_EX[30], OF_EX[29], OF_EX[28], OF_EX[27]);  // AND_Gate
  Multiplexer #(.enable("false")) multiplexer_1 (
    .in0(conflict_detection_unit_2_so_conflict), .in1(1'b0), .out(RW_MA__EX_op2[1]), .sel(and_1_out));
  Conflict_Detection_Unit conflict_detection_unit_3 (
    .A(OF_EX), .B(MA_RW), .FO_Conflict(RW_MA__EX_op1[0]), .SO_Conflict(RW__EX_op2));
  Multiplexer #(.enable("false")) multiplexer_2 (.in0(RW__EX_op2), .in1(1'b0), .out(RW_MA__EX_op2[0]), .sel(and_1_out));
  Conflict_Detection_Unit conflict_detection_unit_4 (
    .A(IF_OF), .B(MA_RW), .FO_Conflict(RW__OF_op1), .SO_Conflict(RW__OF_op2));

  // Notes on the sheet:
  //   RW->MA
  //   MA->EX
  //   RW->EX
  //   RW->OF
endmodule

module Control_Packet (
  input  in_1,
  input  isBgt,
  input  isUBranch,
  input  isLd,
  input  isSt,
  input  in_6,
  input  in_7,
  input  isRet,
  input  [12:0] in_9,
  input  Bubble,
  input  in_11,
  input  in_12,
  output [12:0] out_13,
  output out_14,
  output out_15,
  output out_16,
  output out_17,
  output out_18,
  output out_19,
  output out_20,
  output out_21
);

  wire [7:0] multiplexer_2_out;
  wire [12:0] multiplexer_1_out;

  Register #(.width(1)) register_1 (.D(multiplexer_2_out[7]), .Q(out_14), .clk(in_11), .clr(in_12));  // open: en
  Multiplexer #(.width(13)) multiplexer_1 (
    .in0(in_9), .in1({13{1'b0}}), .out(multiplexer_1_out), .sel(Bubble));  // open: en
  Register #(.width(13)) register_2 (.D(multiplexer_1_out), .Q(out_13), .clk(in_11), .clr(in_12));  // open: en
  Multiplexer #(.width(8), .enable("false")) multiplexer_2 (
    .in0({isRet, in_1, isBgt, isUBranch, isLd, isSt, in_6, in_7}), .in1({8{1'b0}}), .out(multiplexer_2_out),
    .sel(Bubble));
  Register #(.width(1)) register_3 (.D(multiplexer_2_out[6]), .Q(out_15), .clk(in_11), .clr(in_12));  // open: en
  Register #(.width(1)) register_4 (.D(multiplexer_2_out[5]), .Q(out_16), .clk(in_11), .clr(in_12));  // open: en
  Register #(.width(1)) register_5 (.D(multiplexer_2_out[4]), .Q(out_17), .clk(in_11), .clr(in_12));  // open: en
  Register #(.width(1)) register_6 (.D(multiplexer_2_out[3]), .Q(out_18), .clk(in_11), .clr(in_12));  // open: en
  Register #(.width(1)) register_7 (.D(multiplexer_2_out[2]), .Q(out_19), .clk(in_11), .clr(in_12));  // open: en
  Register #(.width(1)) register_8 (.D(multiplexer_2_out[1]), .Q(out_20), .clk(in_11), .clr(in_12));  // open: en
  Register #(.width(1)) register_9 (.D(multiplexer_2_out[0]), .Q(out_21), .clk(in_11), .clr(in_12));  // open: en

  // Notes on the sheet:
  //   ALU Signals
  //   isBeq
  //   isCall
  //   isWb
endmodule

module Check_OPcode_A_op1 (
  input  [4:0] in_1,
  output out_2
);

  wire isBeq_isB__isBgt__is_isCall_out, isNop_out, isNot__isMov_out;

  and isBeq_isB__isBgt__is_isCall (isBeq_isB__isBgt__is_isCall_out, in_1[4], ~in_1[3], ~in_1[2]);  // AND_Gate
  nor nor_1 (out_2, isBeq_isB__isBgt__is_isCall_out, isNop_out, isNot__isMov_out);
  and isNop (isNop_out, ~in_1[4], in_1[3], in_1[2], ~in_1[1], in_1[0]);  // AND_Gate
  and isNot__isMov (isNot__isMov_out, ~in_1[4], in_1[3], ~in_1[1], ~in_1[1]);  // AND_Gate
endmodule

module AshToHash (
);

  wire clock_1_out;
  wire [3:0] undriven;
  wire [31:0] alu_1_aluresult;

  ALU alu_1 (.aluResult(alu_1_aluresult));  // open: A, B, ALUsignals, is, is_2
  Clock clock_1 (.out(clock_1_out));
  Hex_Digit_Display hex_digit_display_1 (.value(undriven));  // open: dp
  _7_Segment_Display u_7_segment_display_1 ();  // open: g, f, a, b, e, d, c, dp
endmodule
